// Logisim project Project.circ as structural Verilog: 37 circuits, main circuit main
module BitComparator (
  input  A,
  input  B,
  input  E,
  input  G,
  output Gout,
  output Eout
);

  wire and_1_out, and_2_out, not_1_out, xnor_1_out;

  not not_1 (not_1_out, B);
  and and_1 (and_1_out, A, not_1_out);
  and and_2 (and_2_out, and_1_out, E);
  xnor xnor_1 (xnor_1_out, A, B);
  or or_1 (Gout, and_2_out, G);
  and and_3 (Eout, xnor_1_out, E);
endmodule

module main (
  output [15:0] out_1,
  output [15:0] out_2,
  output [15:0] out_3,
  output [15:0] out_4,
  output [15:0] out_5,
  output [15:0] out_6,
  output [15:0] out_7,
  output [15:0] out_8,
  output [15:0] out_9,
  output [15:0] out_10,
  output [1:0] out_11,
  output [15:0] out_12,
  output [15:0] out_13,
  output [15:0] out_14,
  output [15:0] out_15,
  output [2:0] out_16,
  output out_17,
  output out_18,
  output out_19,
  output out_20,
  output [15:0] out_21,
  output [1:0] out_22,
  output [5:0] out_23,
  output out_24,
  output [5:0] out_25,
  output out_26,
  output [41:0] out_27,
  output [15:0] out_28,
  output [15:0] out_29,
  output [15:0] out_30,
  output [15:0] out_31,
  output [15:0] out_32,
  output [1:0] out_33,
  output [15:0] out_34,
  output [15:0] out_35,
  output [15:0] out_36,
  output [15:0] out_37,
  output out_38,
  output [15:0] out_39,
  output [15:0] out_40,
  output [15:0] out_41,
  output [15:0] out_42,
  output [15:0] out_43,
  output [15:0] out_44,
  output [15:0] out_45
);

  wire ADDR1MUX, and_2_out, and_3_out, and_4_out, CLK, CLK_BT, d_ff_1_qn, GateALU, GateMARMUX, GateMDR,
       GatePC, LDBEN, LDCC, LDIR, LDMAR, LDMDR, LDPC, LDREG, logic_1_n, logic_1_p, logic_1_z, MARMUX, MIOEN,
       or_2_out, POWER_BUTTON, R, RESET_BUTTON, RW, t_ff_1_q, uc_1_sr2mux;
  wire [1:0] ALUK, SR1MUX;
  wire [2:0] SR1_IN;
  wire [15:0] plus1_1_out_2, sext_5to16_1_out_2, sext_6to16_1_out_2, zext_8to16_1_out_2;

  Button RESET (.out(RESET_BUTTON));
  Button POWER_ON (.out(POWER_BUTTON));
  Clock cl (.out(CLK_BT));
  D_Flip_Flop d_ff_1 (.D(1'b1), .clk(CLK), .Qn(d_ff_1_qn), .reset(POWER_BUTTON));  // open: Q, preset
  T_Flip_Flop t_ff_1 (.T(RESET_BUTTON), .clk(RESET_BUTTON), .Q(t_ff_1_q));  // open: Qn, reset, preset
  T_Flip_Flop t_ff_2 (.T(POWER_BUTTON), .clk(POWER_BUTTON), .Q(out_24));  // open: Qn, reset, preset
  or or_1 (out_26, d_ff_1_qn, t_ff_1_q);
  and and_1 (CLK, out_24, CLK_BT);
  assign out_40 = GateMARMUX ? out_15 : 16'bz;  // Controlled_Buffer controlled_buffer_1
  mux2x1_16Bits mux2x1_16bits_1 (.IO(zext_8to16_1_out_2), .I1(out_28), .SE(MARMUX), .out_4(out_15));
  ZEXT_8to16 zext_8to16_1 (.in_1(out_13[7:0]), .out_2(zext_8to16_1_out_2));
  assign out_40 = GateMDR ? out_10 : 16'bz;  // Controlled_Buffer controlled_buffer_2
  MDR_reg mdr_reg_1 (.LD_MDR(LDMDR), .CLK(CLK), .RES(out_26), .MDR_IN(out_44), .MDR_OUT(out_10));
  mux2x1_16Bits mux2x1_16bits_2 (.IO(out_40), .I1(out_45), .SE(MIOEN), .out_4(out_44));
  SEXT_11to16 sext_11to16_1 (.in_1(out_13[10:0]), .out_2(out_34));
  SEXT_9to16 sext_9to16_1 (.in_1(out_13[8:0]), .out_2(out_37));
  SEXT_6to16 sext_6to16_1 (.in_1(out_13[5:0]), .out_2(sext_6to16_1_out_2));
  IR_Register ir_register_1 (.LD_IR(LDIR), .CLK(CLK), .RES(out_26), .IR_IN(out_40), .IR_OUT(out_13));
  memory memory_1 (
    .CLK(CLK), .MIOEN(MIOEN), .RES(out_26), .RW(RW), .ADDRESS(out_9), .DATO(out_10), .R(R), .MEM_OUT(out_45));
  mux4x1_16Bits mux4x1_16bits_1 (
    .I3(out_34), .I2(out_37), .I1(sext_6to16_1_out_2), .SE(out_33), .I0({16{1'b0}}), .out_6(out_31));
  fullAdder fulladder_1 (.A(out_32), .B(out_31), .R(out_28));
  MAR_reg mar_reg_1 (.LD_MAR(LDMAR), .CLK(CLK), .RES(out_26), .MAR_IN(out_40), .MAR_OUT(out_9));
  and and_2 (and_2_out, out_13[11], out_17);
  and and_3 (and_3_out, out_13[10], out_18);
  and and_4 (and_4_out, out_13[9], out_19);
  mux2x1_16Bits mux2x1_16bits_3 (.IO(out_30), .I1(out_12), .SE(ADDR1MUX), .out_4(out_32));
  or or_2 (or_2_out, and_2_out, and_3_out, and_4_out);
  NZP_reg nzp_reg_1 (
    .P_IN(logic_1_p), .Z_IN(logic_1_z), .N_IN(logic_1_n), .LD(LDCC), .CLK(CLK), .RESET(out_26), .N(out_17),
    .Z(out_18), .P(out_19));
  \logic  logic_1 (.in_1(out_40), .P(logic_1_p), .Z(logic_1_z), .N(logic_1_n));
  assign out_40 = GatePC ? out_12 : 16'bz;  // Controlled_Buffer controlled_buffer_3
  PC_reg pc_reg_1 (.CLK(CLK), .LDPC(LDPC), .RES(out_26), .DIN(out_21), .out_5(out_12));
  mux4x1_16Bits mux4x1_16bits_2 (
    .I2(out_40), .I1(out_28), .SE(out_22), .I0(plus1_1_out_2), .out_6(out_21));  // open: I3
  BEN_reg ben_reg_1 (.D(or_2_out), .LD(LDBEN), .CLK(CLK), .RESET(out_26), .Q(out_20));
  SEXT_5to16 sext_5to16_1 (.in_1(out_13[4:0]), .out_2(sext_5to16_1_out_2));
  plus1 plus1_1 (.in_1(out_12), .out_2(plus1_1_out_2));
  UC uc_1 (
    .IR5(out_13[5]), .INT(1'b0), .R(R), .BEN(out_20), .PSR15(1'b0), .IR15_11(out_13[15:11]), .CLK(CLK),
    .RES(out_26), .NSN(out_25), .CSN(out_23), .SR2MUX(uc_1_sr2mux), .out_12(out_27), .ADDR2MUX(out_33),
    .ADDR1MUX(ADDR1MUX), .SR1MUX(SR1MUX), .DRMUX(out_11), .PCMUX(out_22), .GateMARMUX(GateMARMUX),
    .GateALU(GateALU), .GateMDR(GateMDR), .GatePC(GatePC), .LDPC(LDPC), .LDCC(LDCC), .LDREG(LDREG),
    .LDBEN(LDBEN), .LDIR(LDIR), .LDMDR(LDMDR), .LDMAR(LDMAR), .RW(RW), .MIOEN(MIOEN), .ALUK(ALUK),
    .MARMUX(MARMUX));
  Multiplexer #(.select(2), .width(3)) multiplexer_1 (
    .in0(out_13[11:9]), .in1(3'b110), .in2(3'b111), .out(out_16), .sel(out_11));  // open: in3
  Multiplexer #(.select(2), .width(3)) multiplexer_2 (
    .in0(out_13[11:9]), .in1(out_13[8:6]), .in2(3'b110), .out(SR1_IN), .sel(SR1MUX));  // open: in3
  mux2x1_16Bits mux2x1_16bits_4 (.IO(out_29), .I1(sext_5to16_1_out_2), .SE(uc_1_sr2mux), .out_4(out_35));
  fileRegister fileregister_1 (
    .DR(out_16), .LDREG(LDREG), .CLK(CLK), .RES(out_26), .SR1(SR1_IN), .SR2(out_13[2:0]), .DIN(out_40),
    .R3(out_7), .R4(out_2), .R5(out_4), .R0(out_1), .R6(out_6), .R7(out_8), .R1(out_3), .R2(out_5),
    .SR1OUT(out_30), .SR2OUT(out_29));
  ALU alu_1 (.Selector(ALUK), .A(out_30), .B(out_35), .Result(out_36));
  assign out_40 = GateALU ? out_36 : 16'bz;  // Controlled_Buffer controlled_buffer_4

  assign out_14 = out_12;
  assign out_38 = out_20;
  assign out_39 = out_13;
  assign out_41 = out_10;
  assign out_42 = out_40;
  assign out_43 = out_9;

  // Other names for the same wires on the sheet: ADDR2MUX[1:0] = out_33; BEN = out_20; CSN[5:0] = out_23;
  //   DRMUX[1:0] = out_11; IR[15:0] = out_13; MAR[15:0] = out_9; MDR[15:0] = out_10; N = out_17; NSN[5:0] = out_25;
  //   P = out_19; PC[15:0] = out_12; PCMUX[1:0] = out_22; POWER_ON = out_24; R0[15:0] = out_1; R1[15:0] = out_3;
  //   R2[15:0] = out_5; R3[15:0] = out_7; R4[15:0] = out_2; R5[15:0] = out_4; R6[15:0] = out_6; R7[15:0] = out_8;
  //   RESET = out_26; State[41:0] = out_27; Z = out_18

  // Notes on the sheet:
  //   Ejecuta 15/16 instrucciones. 
  //   No maneja Interrupciones
  //   Autor: Nicolas Sarmiento V.
  //   Littel Computer 3:
  //   Computadora de arquitectura RISC de 16 bits
  //   Controles
endmodule

module AND16 (
  input  in_1,
  input  in_2,
  input  in_3,
  input  in_4,
  input  in_5,
  input  in_6,
  input  in_7,
  input  in_8,
  input  in_9,
  input  in_10,
  input  in_11,
  input  in_12,
  input  in_13,
  input  in_14,
  input  in_15,
  input  in_16,
  output out_17
);

  wire and_1_out, and_2_out, and_3_out, and_4_out, and_5_out, and_6_out, and_7_out, and_8_out, and_9_out,
       and_10_out, and_11_out, and_12_out, and_13_out, and_14_out;

  and and_1 (and_1_out, in_15, in_16);
  and and_2 (and_2_out, in_14, and_1_out);
  and and_3 (and_3_out, in_13, and_2_out);
  and and_4 (and_4_out, in_12, and_3_out);
  and and_5 (and_5_out, in_11, and_4_out);
  and and_6 (and_6_out, in_9, and_7_out);
  and and_7 (and_7_out, in_10, and_5_out);
  and and_8 (and_8_out, in_8, and_6_out);
  and and_9 (and_9_out, in_7, and_8_out);
  and and_10 (and_10_out, in_6, and_9_out);
  and and_11 (and_11_out, in_5, and_10_out);
  and and_12 (and_12_out, in_3, and_13_out);
  and and_13 (and_13_out, in_4, and_11_out);
  and and_14 (and_14_out, in_2, and_12_out);
  and and_15 (out_17, in_1, and_14_out);
endmodule

module Comparator16Bit (
  input  [15:0] A,
  input  [15:0] B,
  output Great,
  output Equal,
  output Less
);

  wire bitcomparator_1_eout, bitcomparator_1_gout, bitcomparator_2_eout, bitcomparator_2_gout,
       bitcomparator_3_eout, bitcomparator_3_gout, bitcomparator_4_eout, bitcomparator_4_gout,
       bitcomparator_5_eout, bitcomparator_5_gout, bitcomparator_6_eout, bitcomparator_6_gout,
       bitcomparator_7_eout, bitcomparator_7_gout, bitcomparator_8_eout, bitcomparator_8_gout,
       bitcomparator_9_eout, bitcomparator_9_gout, bitcomparator_10_eout, bitcomparator_10_gout,
       bitcomparator_11_eout, bitcomparator_11_gout, bitcomparator_12_eout, bitcomparator_12_gout,
       bitcomparator_13_eout, bitcomparator_13_gout, bitcomparator_14_eout, bitcomparator_14_gout,
       bitcomparator_15_eout, bitcomparator_15_gout, bitcomparator_16_eout, bitcomparator_16_gout, not_1_out,
       xor_1_out;

  BitComparator bitcomparator_1 (
    .A(A[0]), .B(B[0]), .E(bitcomparator_2_eout), .G(bitcomparator_2_gout), .Gout(bitcomparator_1_gout),
    .Eout(bitcomparator_1_eout));
  BitComparator bitcomparator_2 (
    .A(A[1]), .B(B[1]), .E(bitcomparator_3_eout), .G(bitcomparator_3_gout), .Gout(bitcomparator_2_gout),
    .Eout(bitcomparator_2_eout));
  BitComparator bitcomparator_3 (
    .A(A[2]), .B(B[2]), .E(bitcomparator_4_eout), .G(bitcomparator_4_gout), .Gout(bitcomparator_3_gout),
    .Eout(bitcomparator_3_eout));
  BitComparator bitcomparator_4 (
    .A(A[3]), .B(B[3]), .E(bitcomparator_5_eout), .G(bitcomparator_5_gout), .Gout(bitcomparator_4_gout),
    .Eout(bitcomparator_4_eout));
  BitComparator bitcomparator_5 (
    .A(A[4]), .B(B[4]), .E(bitcomparator_6_eout), .G(bitcomparator_6_gout), .Gout(bitcomparator_5_gout),
    .Eout(bitcomparator_5_eout));
  BitComparator bitcomparator_6 (
    .A(A[5]), .B(B[5]), .E(bitcomparator_7_eout), .G(bitcomparator_7_gout), .Gout(bitcomparator_6_gout),
    .Eout(bitcomparator_6_eout));
  BitComparator bitcomparator_7 (
    .A(A[6]), .B(B[6]), .E(bitcomparator_8_eout), .G(bitcomparator_8_gout), .Gout(bitcomparator_7_gout),
    .Eout(bitcomparator_7_eout));
  BitComparator bitcomparator_8 (
    .A(A[7]), .B(B[7]), .E(bitcomparator_9_eout), .G(bitcomparator_9_gout), .Gout(bitcomparator_8_gout),
    .Eout(bitcomparator_8_eout));
  BitComparator bitcomparator_9 (
    .A(A[8]), .B(B[8]), .E(bitcomparator_10_eout), .G(bitcomparator_10_gout), .Gout(bitcomparator_9_gout),
    .Eout(bitcomparator_9_eout));
  BitComparator bitcomparator_10 (
    .A(A[9]), .B(B[9]), .E(bitcomparator_11_eout), .G(bitcomparator_11_gout), .Gout(bitcomparator_10_gout),
    .Eout(bitcomparator_10_eout));
  BitComparator bitcomparator_11 (
    .A(A[10]), .B(B[10]), .E(bitcomparator_12_eout), .G(bitcomparator_12_gout), .Gout(bitcomparator_11_gout),
    .Eout(bitcomparator_11_eout));
  BitComparator bitcomparator_12 (
    .A(A[11]), .B(B[11]), .E(bitcomparator_13_eout), .G(bitcomparator_13_gout), .Gout(bitcomparator_12_gout),
    .Eout(bitcomparator_12_eout));
  BitComparator bitcomparator_13 (
    .A(A[12]), .B(B[12]), .E(bitcomparator_14_eout), .G(bitcomparator_14_gout), .Gout(bitcomparator_13_gout),
    .Eout(bitcomparator_13_eout));
  BitComparator bitcomparator_14 (
    .A(A[13]), .B(B[13]), .E(bitcomparator_15_eout), .G(bitcomparator_15_gout), .Gout(bitcomparator_14_gout),
    .Eout(bitcomparator_14_eout));
  BitComparator bitcomparator_15 (
    .A(A[14]), .B(B[14]), .E(bitcomparator_16_eout), .G(bitcomparator_16_gout), .Gout(bitcomparator_15_gout),
    .Eout(bitcomparator_15_eout));
  BitComparator bitcomparator_16 (
    .A(A[15]), .B(B[15]), .E(1'b1), .G(1'b0), .Gout(bitcomparator_16_gout), .Eout(bitcomparator_16_eout));
  not not_1 (not_1_out, bitcomparator_1_gout);
  xor xor_1 (xor_1_out, A[15], B[15]);
  Multiplexer multiplexer_1 (.in0(bitcomparator_1_gout), .in1(not_1_out), .out(Great), .sel(xor_1_out));
  AND16 and16_1 (
    .in_1(bitcomparator_1_eout), .in_2(bitcomparator_2_eout), .in_3(bitcomparator_3_eout),
    .in_4(bitcomparator_4_eout), .in_5(bitcomparator_5_eout), .in_6(bitcomparator_6_eout),
    .in_7(bitcomparator_7_eout), .in_8(bitcomparator_8_eout), .in_9(bitcomparator_9_eout),
    .in_10(bitcomparator_10_eout), .in_11(bitcomparator_11_eout), .in_12(bitcomparator_12_eout),
    .in_13(bitcomparator_13_eout), .in_14(bitcomparator_14_eout), .in_15(bitcomparator_15_eout),
    .in_16(bitcomparator_16_eout), .out_17(Equal));
  nor nor_1 (Less, Great, Equal);
endmodule

module ALU_Taller (
  input  [15:0] A,
  input  [15:0] B,
  input  [2:0] Selector,
  output P,
  output Z,
  output N,
  output [15:0] Result,
  output Overflow
);

  wire adder16bits_1_c_out, adder16bits_1_penult_carry_out, comparator16bit_1_equal, or_1_out,
       subs16bits_1_cout, subs16bits_1_pcarry, xor_1_out, xor_2_out;
  wire [15:0] adder16bits_1_sum, and16bitwise_1_r, not16bitwise_1_r, not16bitwise_2_r, or16bitwise_1_r,
       subs16bits_1_r;

  Adder16Bits adder16bits_1 (
    .A(A), .B(B), .C_Out(adder16bits_1_c_out), .penult_carry_out(adder16bits_1_penult_carry_out),
    .Sum(adder16bits_1_sum));
  xor xor_1 (xor_1_out, adder16bits_1_c_out, adder16bits_1_penult_carry_out);
  subs16Bits subs16bits_1 (.A(A), .B(B), .R(subs16bits_1_r), .Cout(subs16bits_1_cout), .Pcarry(subs16bits_1_pcarry));
  xor xor_2 (xor_2_out, subs16bits_1_pcarry, subs16bits_1_cout);
  or or_1 (or_1_out, xor_2_out, comparator16bit_1_equal);
  AND16Bitwise and16bitwise_1 (.A(A), .B(B), .R(and16bitwise_1_r));
  mux8x1 mux8x1_1 (
    .S(Selector), .A(xor_1_out), .B(or_1_out), .C(1'b0), .D(1'b0), .E(1'b0), .F(1'b0), .G(1'b0), .H(1'b0),
    .o(Overflow));
  OR16Bitwise or16bitwise_1 (.A(A), .B(B), .R(or16bitwise_1_r));
  Multiplexer #(.select(3), .width(16)) multiplexer_1 (
    .in0(adder16bits_1_sum), .in1(subs16bits_1_r), .in2(and16bitwise_1_r), .in3(or16bitwise_1_r),
    .in4(not16bitwise_1_r), .in5(not16bitwise_2_r), .in6(A), .in7(B), .out(Result), .sel(Selector));
  Comparator16Bit comparator16bit_1 (.A(B), .B(16'h8000), .Equal(comparator16bit_1_equal));  // open: Less, Great
  NOT16Bitwise not16bitwise_1 (.A(A), .R(not16bitwise_1_r));
  Comparator16Bit comparator16bit_2 (.A(Result), .B({16{1'b0}}), .Less(N), .Great(P), .Equal(Z));
  NOT16Bitwise not16bitwise_2 (.A(B), .R(not16bitwise_2_r));

  // Notes on the sheet:
  //   0 : Suma
  //   1 : Resta
  //   2 :AND Bitwise
  //   3 :OR Bitwise
  //   4 :NOT A
  //   5 :NOT B
  //   6: A
  //   7: B
endmodule

module bitAdd (
  input  A,
  input  B,
  input  CarryIn,
  output Sum,
  output CarryOut
);

  wire and_1_out, and_2_out, xor_1_out;

  xor xor_1 (xor_1_out, A, B);
  and and_1 (and_1_out, xor_1_out, CarryIn);
  and and_2 (and_2_out, A, B);
  xor xor_2 (Sum, xor_1_out, CarryIn);
  or or_1 (CarryOut, and_1_out, and_2_out);
endmodule

module Adder16Bits (
  input  [15:0] A,
  input  [15:0] B,
  output C_Out,
  output penult_carry_out,
  output [15:0] Sum
);

  wire N00_carryout, N01_carryout, N02_carryout, N03_carryout, N04_carryout, N05_carryout, N06_carryout,
       N07_carryout, N08_carryout, N09_carryout, N10_carryout, N11_carryout, N12_carryout, N13_carryout;

  bitAdd N15 (.B(A[15]), .CarryIn(penult_carry_out), .A(B[15]), .Sum(Sum[15]), .CarryOut(C_Out));
  bitAdd N14 (.B(A[14]), .CarryIn(N13_carryout), .A(B[14]), .Sum(Sum[14]), .CarryOut(penult_carry_out));
  bitAdd N13 (.B(A[13]), .CarryIn(N12_carryout), .A(B[13]), .Sum(Sum[13]), .CarryOut(N13_carryout));
  bitAdd N12 (.B(A[12]), .CarryIn(N11_carryout), .A(B[12]), .Sum(Sum[12]), .CarryOut(N12_carryout));
  bitAdd N11 (.B(A[11]), .CarryIn(N10_carryout), .A(B[11]), .Sum(Sum[11]), .CarryOut(N11_carryout));
  bitAdd N10 (.B(A[10]), .CarryIn(N09_carryout), .A(B[10]), .Sum(Sum[10]), .CarryOut(N10_carryout));
  bitAdd N09 (.B(A[9]), .CarryIn(N08_carryout), .A(B[9]), .Sum(Sum[9]), .CarryOut(N09_carryout));
  bitAdd N08 (.B(A[8]), .CarryIn(N07_carryout), .A(B[8]), .Sum(Sum[8]), .CarryOut(N08_carryout));
  bitAdd N07 (.B(A[7]), .CarryIn(N06_carryout), .A(B[7]), .Sum(Sum[7]), .CarryOut(N07_carryout));
  bitAdd N06 (.B(A[6]), .CarryIn(N05_carryout), .A(B[6]), .Sum(Sum[6]), .CarryOut(N06_carryout));
  bitAdd N05 (.B(A[5]), .CarryIn(N04_carryout), .A(B[5]), .Sum(Sum[5]), .CarryOut(N05_carryout));
  bitAdd N04 (.B(A[4]), .CarryIn(N03_carryout), .A(B[4]), .Sum(Sum[4]), .CarryOut(N04_carryout));
  bitAdd N03 (.B(A[3]), .CarryIn(N02_carryout), .A(B[3]), .Sum(Sum[3]), .CarryOut(N03_carryout));
  bitAdd N02 (.B(A[2]), .CarryIn(N01_carryout), .A(B[2]), .Sum(Sum[2]), .CarryOut(N02_carryout));
  bitAdd N01 (.B(A[1]), .CarryIn(N00_carryout), .A(B[1]), .Sum(Sum[1]), .CarryOut(N01_carryout));
  bitAdd N00 (.B(A[0]), .A(B[0]), .Sum(Sum[0]), .CarryOut(N00_carryout));  // open: CarryIn
endmodule

module AND16Bitwise (
  input  [15:0] A,
  input  [15:0] B,
  output [15:0] R
);

  and and_1 (R[15], B[15], A[15]);
  and and_2 (R[14], B[14], A[14]);
  and and_3 (R[13], B[13], A[13]);
  and and_4 (R[12], B[12], A[12]);
  and and_5 (R[11], B[11], A[11]);
  and and_6 (R[10], B[10], A[10]);
  and and_7 (R[9], B[9], A[9]);
  and and_8 (R[8], B[8], A[8]);
  and and_9 (R[7], B[7], A[7]);
  and and_10 (R[6], B[6], A[6]);
  and and_11 (R[5], B[5], A[5]);
  and and_12 (R[4], B[4], A[4]);
  and and_13 (R[3], B[3], A[3]);
  and and_14 (R[2], B[2], A[2]);
  and and_15 (R[1], B[1], A[1]);
  and and_16 (R[0], B[0], A[0]);
endmodule

module OR16Bitwise (
  input  [15:0] A,
  input  [15:0] B,
  output [15:0] R
);

  or or_1 (R[15], B[15], A[15]);
  or or_2 (R[14], B[14], A[14]);
  or or_3 (R[13], B[13], A[13]);
  or or_4 (R[12], B[12], A[12]);
  or or_5 (R[11], B[11], A[11]);
  or or_6 (R[10], B[10], A[10]);
  or or_7 (R[9], B[9], A[9]);
  or or_8 (R[8], B[8], A[8]);
  or or_9 (R[7], B[7], A[7]);
  or or_10 (R[6], B[6], A[6]);
  or or_11 (R[5], B[5], A[5]);
  or or_12 (R[4], B[4], A[4]);
  or or_13 (R[3], B[3], A[3]);
  or or_14 (R[2], B[2], A[2]);
  or or_15 (R[1], B[1], A[1]);
  or or_16 (R[0], B[0], A[0]);
endmodule

module XOR16Bitwise (
  input  [15:0] A,
  input  [15:0] B,
  output [15:0] R
);

  xor xor_1 (R[15], B[15], A[15]);
  xor xor_2 (R[14], B[14], A[14]);
  xor xor_3 (R[13], B[13], A[13]);
  xor xor_4 (R[12], B[12], A[12]);
  xor xor_5 (R[11], B[11], A[11]);
  xor xor_6 (R[10], B[10], A[10]);
  xor xor_7 (R[9], B[9], A[9]);
  xor xor_8 (R[8], B[8], A[8]);
  xor xor_9 (R[7], B[7], A[7]);
  xor xor_10 (R[6], B[6], A[6]);
  xor xor_11 (R[5], B[5], A[5]);
  xor xor_12 (R[4], B[4], A[4]);
  xor xor_13 (R[3], B[3], A[3]);
  xor xor_14 (R[2], B[2], A[2]);
  xor xor_15 (R[1], B[1], A[1]);
  xor xor_16 (R[0], B[0], A[0]);
endmodule

module NOT16Bitwise (
  input  [15:0] A,
  output [15:0] R
);

  not not_1 (R[15], A[15]);
  not not_2 (R[14], A[14]);
  not not_3 (R[13], A[13]);
  not not_4 (R[12], A[12]);
  not not_5 (R[11], A[11]);
  not not_6 (R[10], A[10]);
  not not_7 (R[9], A[9]);
  not not_8 (R[8], A[8]);
  not not_9 (R[7], A[7]);
  not not_10 (R[6], A[6]);
  not not_11 (R[5], A[5]);
  not not_12 (R[4], A[4]);
  not not_13 (R[3], A[3]);
  not not_14 (R[2], A[2]);
  not not_15 (R[1], A[1]);
  not not_16 (R[0], A[0]);
endmodule

module subs16Bits (
  input  [15:0] A,
  input  [15:0] B,
  output Cout,
  output Pcarry,
  output [15:0] R
);

  wire [15:0] adder16bits_2_sum, xor16bitwise_1_r;

  Adder16Bits adder16bits_1 (.A(A), .B(adder16bits_2_sum), .C_Out(Cout), .penult_carry_out(Pcarry), .Sum(R));
  Adder16Bits adder16bits_2 (
    .A(16'h1), .B(xor16bitwise_1_r), .Sum(adder16bits_2_sum));  // open: C_Out, penult_carry_out
  XOR16Bitwise xor16bitwise_1 (.A({16{1'b1}}), .B(B), .R(xor16bitwise_1_r));
endmodule

module mux2x1 (
  input  A,
  input  B,
  input  S,
  output out_4
);

  wire and_1_out, and_2_out, not_1_out;

  not not_1 (not_1_out, S);
  and and_1 (and_1_out, A, not_1_out);
  and and_2 (and_2_out, B, S);
  or or_1 (out_4, and_1_out, and_2_out);
endmodule

module mux8x1 (
  input  A,
  input  B,
  input  C,
  input  D,
  input  E,
  input  F,
  input  G,
  input  H,
  input  [2:0] S,
  output o
);

  wire and_1_out, and_2_out, and_3_out, and_4_out, and_5_out, and_6_out, and_7_out, and_8_out, and_9_out,
       and_10_out, and_11_out, and_12_out, and_13_out, and_14_out, and_15_out, and_16_out, and_17_out,
       and_18_out, and_19_out, and_20_out, and_21_out, and_22_out, and_23_out, and_24_out, not_1_out,
       not_2_out, not_3_out, not_4_out, not_5_out, not_6_out, not_7_out, not_8_out, not_9_out, not_10_out,
       not_11_out, not_12_out, or_1_out, or_2_out, or_3_out, or_4_out, or_5_out, or_6_out;

  not not_1 (not_1_out, S[0]);
  not not_2 (not_2_out, S[0]);
  not not_3 (not_3_out, S[0]);
  not not_4 (not_4_out, S[0]);
  and and_1 (and_1_out, A, not_1_out);
  not not_5 (not_5_out, S[1]);
  and and_2 (and_2_out, B, S[0]);
  not not_6 (not_6_out, S[1]);
  and and_3 (and_3_out, C, not_2_out);
  and and_4 (and_4_out, D, S[0]);
  and and_5 (and_5_out, E, not_3_out);
  not not_7 (not_7_out, S[1]);
  and and_6 (and_6_out, F, S[0]);
  not not_8 (not_8_out, S[1]);
  and and_7 (and_7_out, G, not_4_out);
  and and_8 (and_8_out, H, S[0]);
  and and_9 (and_9_out, and_1_out, not_5_out);
  and and_10 (and_10_out, and_2_out, not_6_out);
  and and_11 (and_11_out, and_3_out, S[1]);
  and and_12 (and_12_out, and_4_out, S[1]);
  and and_13 (and_13_out, and_5_out, not_7_out);
  and and_14 (and_14_out, and_6_out, not_8_out);
  and and_15 (and_15_out, and_7_out, S[1]);
  and and_16 (and_16_out, and_8_out, S[1]);
  and and_17 (and_17_out, and_9_out, not_9_out);
  not not_9 (not_9_out, S[2]);
  and and_18 (and_18_out, and_10_out, not_10_out);
  not not_10 (not_10_out, S[2]);
  and and_19 (and_19_out, and_11_out, not_11_out);
  not not_11 (not_11_out, S[2]);
  and and_20 (and_20_out, and_12_out, not_12_out);
  not not_12 (not_12_out, S[2]);
  and and_21 (and_21_out, and_13_out, S[2]);
  buf and_22 (and_22_out, and_14_out);  // AND_Gate
  and and_23 (and_23_out, and_15_out, S[2]);
  and and_24 (and_24_out, and_16_out, S[2]);
  or or_1 (or_1_out, and_17_out, and_18_out);
  or or_2 (or_2_out, and_19_out, and_20_out);
  or or_3 (or_3_out, and_21_out, and_22_out);
  or or_4 (or_4_out, and_23_out, and_24_out);
  or or_5 (or_5_out, or_1_out, or_2_out);
  or or_6 (or_6_out, or_3_out, or_4_out);
  or or_7 (o, or_5_out, or_6_out);
endmodule

module testComparator (
  input  [15:0] in_1,
  input  [15:0] in_2,
  input  [15:0] in_3,
  input  [15:0] in_4,
  input  [15:0] in_5,
  input  [15:0] in_6,
  input  [15:0] in_7,
  input  [15:0] in_8,
  output out_9,
  output out_10,
  output out_11,
  output out_12,
  output out_13,
  output out_14,
  output out_15,
  output out_16,
  output out_17,
  output out_18,
  output out_19,
  output out_20
);

  Comparator16Bit comparator16bit_1 (.A(in_1), .B(in_3), .Less(out_13), .Great(out_9), .Equal(out_11));
  Comparator16Bit comparator16bit_2 (.A(in_6), .B(in_8), .Less(out_20), .Great(out_16), .Equal(out_18));
  Comparator16Bit comparator16bit_3 (.A(in_2), .B(in_4), .Less(out_14), .Great(out_10), .Equal(out_12));
  Comparator16Bit comparator16bit_4 (.A(in_5), .B(in_7), .Less(out_19), .Great(out_15), .Equal(out_17));
endmodule

module PriotyEncoder4to2 (
  input  I0,
  input  I1,
  input  I2,
  input  I3,
  output V,
  output Y0,
  output Y1
);

  wire and_1_out, not_1_out;

  not not_1 (not_1_out, I2);
  and and_1 (and_1_out, I1, not_1_out);
  or or_1 (V, I0, I1, I2, I3);
  or or_2 (Y0, and_1_out, I3);
  or or_3 (Y1, I2, I3);
endmodule

module mux4x1 (
  input  in_1,
  input  in_2,
  input  in_3,
  input  in_4,
  input  [1:0] in_5,
  output out_6
);

  wire and_1_out, and_2_out, and_3_out, and_4_out, and_5_out, and_6_out, and_7_out, and_8_out, not_1_out,
       not_2_out, not_3_out, not_4_out, or_1_out, or_2_out;

  not not_1 (not_1_out, in_5[0]);
  not not_2 (not_2_out, in_5[0]);
  and and_1 (and_1_out, in_1, not_1_out);
  and and_2 (and_2_out, in_2, in_5[0]);
  and and_3 (and_3_out, in_3, not_2_out);
  and and_4 (and_4_out, in_4, in_5[0]);
  not not_3 (not_3_out, in_5[1]);
  not not_4 (not_4_out, in_5[1]);
  and and_5 (and_5_out, and_1_out, not_3_out);
  and and_6 (and_6_out, and_2_out, not_4_out);
  and and_7 (and_7_out, and_3_out, in_5[1]);
  and and_8 (and_8_out, and_4_out, in_5[1]);
  or or_1 (or_1_out, and_5_out, and_6_out);
  or or_2 (or_2_out, and_7_out, and_8_out);
  or or_3 (out_6, or_1_out, or_2_out);
endmodule

module mux4x1_16Bits (
  input  [1:0] SE,
  input  [15:0] I0,
  input  [15:0] I1,
  input  [15:0] I2,
  input  [15:0] I3,
  output [15:0] out_6
);

  mux4x1 mux4x1_1 (.in_1(I0[0]), .in_2(I1[0]), .in_3(I2[0]), .in_4(I3[0]), .in_5(SE), .out_6(out_6[0]));
  mux4x1 mux4x1_2 (.in_1(I0[1]), .in_2(I1[1]), .in_3(I2[1]), .in_4(I3[1]), .in_5(SE), .out_6(out_6[1]));
  mux4x1 mux4x1_3 (.in_1(I0[2]), .in_2(I1[2]), .in_3(I2[2]), .in_4(I3[2]), .in_5(SE), .out_6(out_6[2]));
  mux4x1 mux4x1_4 (.in_1(I0[3]), .in_2(I1[3]), .in_3(I2[3]), .in_4(I3[3]), .in_5(SE), .out_6(out_6[3]));
  mux4x1 mux4x1_5 (.in_1(I0[4]), .in_2(I1[4]), .in_3(I2[4]), .in_4(I3[4]), .in_5(SE), .out_6(out_6[4]));
  mux4x1 mux4x1_6 (.in_1(I0[5]), .in_2(I1[5]), .in_3(I2[5]), .in_4(I3[5]), .in_5(SE), .out_6(out_6[5]));
  mux4x1 mux4x1_7 (.in_1(I0[6]), .in_2(I1[6]), .in_3(I2[6]), .in_4(I3[6]), .in_5(SE), .out_6(out_6[6]));
  mux4x1 mux4x1_8 (.in_1(I0[7]), .in_2(I1[7]), .in_3(I2[7]), .in_4(I3[7]), .in_5(SE), .out_6(out_6[7]));
  mux4x1 mux4x1_9 (.in_1(I0[8]), .in_2(I1[8]), .in_3(I2[8]), .in_4(I3[8]), .in_5(SE), .out_6(out_6[8]));
  mux4x1 mux4x1_10 (.in_1(I0[9]), .in_2(I1[9]), .in_3(I2[9]), .in_4(I3[9]), .in_5(SE), .out_6(out_6[9]));
  mux4x1 mux4x1_11 (.in_1(I0[10]), .in_2(I1[10]), .in_3(I2[10]), .in_4(I3[10]), .in_5(SE), .out_6(out_6[10]));
  mux4x1 mux4x1_12 (.in_1(I0[11]), .in_2(I1[11]), .in_3(I2[11]), .in_4(I3[11]), .in_5(SE), .out_6(out_6[11]));
  mux4x1 mux4x1_13 (.in_1(I0[12]), .in_2(I1[12]), .in_3(I2[12]), .in_4(I3[12]), .in_5(SE), .out_6(out_6[12]));
  mux4x1 mux4x1_14 (.in_1(I0[13]), .in_2(I1[13]), .in_3(I2[13]), .in_4(I3[13]), .in_5(SE), .out_6(out_6[13]));
  mux4x1 mux4x1_15 (.in_1(I0[14]), .in_2(I1[14]), .in_3(I2[14]), .in_4(I3[14]), .in_5(SE), .out_6(out_6[14]));
  mux4x1 mux4x1_16 (.in_1(I0[15]), .in_2(I1[15]), .in_3(I2[15]), .in_4(I3[15]), .in_5(SE), .out_6(out_6[15]));
endmodule

module mux2x1_16Bits (
  input  SE,
  input  [15:0] IO,
  input  [15:0] I1,
  output [15:0] out_4
);

  mux2x1 mux2x1_1 (.A(IO[0]), .B(I1[0]), .S(SE), .out_4(out_4[0]));
  mux2x1 mux2x1_2 (.A(IO[1]), .B(I1[1]), .S(SE), .out_4(out_4[1]));
  mux2x1 mux2x1_3 (.A(IO[2]), .B(I1[2]), .S(SE), .out_4(out_4[2]));
  mux2x1 mux2x1_4 (.A(IO[3]), .B(I1[3]), .S(SE), .out_4(out_4[3]));
  mux2x1 mux2x1_5 (.A(IO[4]), .B(I1[4]), .S(SE), .out_4(out_4[4]));
  mux2x1 mux2x1_6 (.A(IO[5]), .B(I1[5]), .S(SE), .out_4(out_4[5]));
  mux2x1 mux2x1_7 (.A(IO[6]), .B(I1[6]), .S(SE), .out_4(out_4[6]));
  mux2x1 mux2x1_8 (.A(IO[7]), .B(I1[7]), .S(SE), .out_4(out_4[7]));
  mux2x1 mux2x1_9 (.A(IO[8]), .B(I1[8]), .S(SE), .out_4(out_4[8]));
  mux2x1 mux2x1_10 (.A(IO[9]), .B(I1[9]), .S(SE), .out_4(out_4[9]));
  mux2x1 mux2x1_11 (.A(IO[10]), .B(I1[10]), .S(SE), .out_4(out_4[10]));
  mux2x1 mux2x1_12 (.A(IO[11]), .B(I1[11]), .S(SE), .out_4(out_4[11]));
  mux2x1 mux2x1_13 (.A(IO[12]), .B(I1[12]), .S(SE), .out_4(out_4[12]));
  mux2x1 mux2x1_14 (.A(IO[13]), .B(I1[13]), .S(SE), .out_4(out_4[13]));
  mux2x1 mux2x1_15 (.A(IO[14]), .B(I1[14]), .S(SE), .out_4(out_4[14]));
  mux2x1 mux2x1_16 (.A(IO[15]), .B(I1[15]), .S(SE), .out_4(out_4[15]));
endmodule

module ZEXT_8to16 (
  input  [7:0] in_1,
  output [15:0] out_2
);


  assign out_2 = {{8{1'b0}}, in_1};
endmodule

module SEXT_11to16 (
  input  [10:0] in_1,
  output [15:0] out_2
);


  assign out_2 = {{6{in_1[10]}}, in_1[9:0]};

  // Notes on the sheet:
  //   11 bit Sign ext
endmodule

module SEXT_9to16 (
  input  [8:0] in_1,
  output [15:0] out_2
);


  assign out_2 = {{8{in_1[8]}}, in_1[7:0]};
endmodule

module SEXT_6to16 (
  input  [5:0] in_1,
  output [15:0] out_2
);


  assign out_2 = {{11{in_1[5]}}, in_1[4:0]};
endmodule

module SEXT_5to16 (
  input  [4:0] in_1,
  output [15:0] out_2
);


  assign out_2 = {{12{in_1[4]}}, in_1[3:0]};
endmodule

module fullAdder (
  input  [15:0] A,
  input  [15:0] B,
  output [15:0] R
);

  Adder16Bits adder16bits_1 (.A(A), .B(B), .Sum(R));  // open: C_Out, penult_carry_out
endmodule

module plus1 (
  input  [15:0] in_1,
  output [15:0] out_2
);

  Adder16Bits adder16bits_1 (.A(in_1), .B(16'h1), .Sum(out_2));  // open: C_Out, penult_carry_out
endmodule

module ALU (
  input  [15:0] A,
  input  [15:0] B,
  input  [1:0] Selector,
  output [15:0] Result
);

  wire [15:0] adder16bits_1_sum, and16bitwise_1_r, not16bitwise_1_r;

  Adder16Bits adder16bits_1 (.A(A), .B(B), .Sum(adder16bits_1_sum));  // open: C_Out, penult_carry_out
  AND16Bitwise and16bitwise_1 (.A(A), .B(B), .R(and16bitwise_1_r));
  Multiplexer #(.select(2), .width(16)) multiplexer_1 (
    .in0(adder16bits_1_sum), .in1(and16bitwise_1_r), .in2(not16bitwise_1_r), .in3(A), .out(Result),
    .sel(Selector));
  NOT16Bitwise not16bitwise_1 (.A(A), .R(not16bitwise_1_r));

  // Notes on the sheet:
  //   3 :A
  //   0 : Suma
  //   1 : AND bitwise
  //   2 :NOT A
endmodule

module \logic  (
  input  [15:0] in_1,
  output P,
  output Z,
  output N
);

  Comparator16Bit comparator16bit_1 (.A(in_1), .B({16{1'b0}}), .Less(N), .Great(P), .Equal(Z));
endmodule

module fileRegister (
  input  [15:0] DIN,
  input  [2:0] DR,
  input  LDREG,
  input  CLK,
  input  RES,
  input  [2:0] SR1,
  input  [2:0] SR2,
  output [15:0] R0,
  output [15:0] R1,
  output [15:0] R2,
  output [15:0] R3,
  output [15:0] R4,
  output [15:0] R5,
  output [15:0] R6,
  output [15:0] R7,
  output [15:0] SR1OUT,
  output [15:0] SR2OUT
);

  wire and_1_out, and_2_out, and_3_out, and_4_out, and_5_out, and_6_out, and_7_out, and_8_out,
       decoder_1_out0, decoder_1_out1, decoder_1_out2, decoder_1_out3, decoder_1_out4, decoder_1_out5,
       decoder_1_out6, decoder_1_out7;

  Decoder #(.select(3)) decoder_1 (
    .out0(decoder_1_out0), .out1(decoder_1_out1), .out2(decoder_1_out2), .out3(decoder_1_out3),
    .out4(decoder_1_out4), .out5(decoder_1_out5), .out6(decoder_1_out6), .out7(decoder_1_out7), .sel(DR));  // open: en
  and and_1 (and_1_out, decoder_1_out0, LDREG);
  and and_2 (and_2_out, decoder_1_out1, LDREG);
  and and_3 (and_3_out, decoder_1_out2, LDREG);
  and and_4 (and_4_out, decoder_1_out3, LDREG);
  and and_5 (and_5_out, decoder_1_out4, LDREG);
  and and_6 (and_6_out, decoder_1_out5, LDREG);
  and and_7 (and_7_out, decoder_1_out6, LDREG);
  and and_8 (and_8_out, decoder_1_out7, LDREG);
  Register #(.width(16)) register_1 (.D(DIN), .en(and_1_out), .clk(CLK), .Q(R0), .clr(RES));
  Register #(.width(16)) register_2 (.D(DIN), .en(and_2_out), .clk(CLK), .Q(R1), .clr(RES));
  Register #(.width(16)) register_3 (.D(DIN), .en(and_3_out), .clk(CLK), .Q(R2), .clr(RES));
  Register #(.width(16)) register_4 (.D(DIN), .en(and_4_out), .clk(CLK), .Q(R3), .clr(RES));
  Register #(.width(16)) register_5 (.D(DIN), .en(and_5_out), .clk(CLK), .Q(R4), .clr(RES));
  Register #(.width(16)) register_6 (.D(DIN), .en(and_6_out), .clk(CLK), .Q(R5), .clr(RES));
  Register #(.width(16)) register_7 (.D(DIN), .en(and_7_out), .clk(CLK), .Q(R6), .clr(RES));
  Register #(.width(16)) register_8 (.D(DIN), .en(and_8_out), .clk(CLK), .Q(R7), .clr(RES));
  Multiplexer #(.select(3), .width(16)) multiplexer_1 (
    .in0(R0), .in1(R1), .in2(R2), .in3(R3), .in4(R4), .in5(R5), .in6(R6), .in7(R7), .out(SR2OUT), .sel(SR2));
  Multiplexer #(.select(3), .width(16)) multiplexer_2 (
    .in0(R0), .in1(R1), .in2(R2), .in3(R3), .in4(R4), .in5(R5), .in6(R6), .in7(R7), .out(SR1OUT), .sel(SR1));
endmodule

module MAR_reg (
  input  [15:0] MAR_IN,
  input  LD_MAR,
  input  CLK,
  input  RES,
  output [15:0] MAR_OUT
);

  Register #(.width(16)) register_1 (.D(MAR_IN), .en(LD_MAR), .clk(CLK), .Q(MAR_OUT), .clr(RES));
endmodule

module IR_Register (
  input  [15:0] IR_IN,
  input  LD_IR,
  input  CLK,
  input  RES,
  output [15:0] IR_OUT
);

  Register #(.width(16)) register_1 (.D(IR_IN), .en(LD_IR), .clk(CLK), .Q(IR_OUT), .clr(RES));
endmodule

module MDR_reg (
  input  [15:0] MDR_IN,
  input  LD_MDR,
  input  CLK,
  input  RES,
  output [15:0] MDR_OUT
);

  Register #(.width(16)) register_1 (.D(MDR_IN), .en(LD_MDR), .clk(CLK), .Q(MDR_OUT), .clr(RES));
endmodule

module PC_reg (
  input  [15:0] DIN,
  input  RES,
  input  LDPC,
  input  CLK,
  output [15:0] out_5
);

  wire or_1_out;
  wire [15:0] multiplexer_1_out;

  or or_1 (or_1_out, RES, LDPC);
  Multiplexer #(.width(16)) multiplexer_1 (.in0(DIN), .in1(16'h3000), .out(multiplexer_1_out), .sel(RES));
  Register #(.width(16)) register_1 (.D(multiplexer_1_out), .en(or_1_out), .clk(CLK), .Q(out_5), .clr(1'b0));
endmodule

module UC (
  input  INT,
  input  R,
  input  BEN,
  input  PSR15,
  input  [4:0] IR15_11,
  input  CLK,
  input  RES,
  input  IR5,
  output SR2MUX,
  output [5:0] NSN,
  output [5:0] CSN,
  output [41:0] out_12,
  output RW,
  output MIOEN,
  output [1:0] ALUK,
  output MARMUX,
  output [1:0] ADDR2MUX,
  output ADDR1MUX,
  output [1:0] SR1MUX,
  output [1:0] DRMUX,
  output [1:0] PCMUX,
  output GateMARMUX,
  output GateALU,
  output GateMDR,
  output GatePC,
  output LDPC,
  output LDCC,
  output LDREG,
  output LDBEN,
  output LDIR,
  output LDMDR,
  output LDMAR
);

  wire and_1_out, and_2_out, and_3_out, and_4_out, and_5_out, COND0, COND1, COND2, IRD, J0, J1, J2, J3, J4,
       J5;
  wire [4:0] or_5_out;
  wire [5:0] multiplexer_1_out;
  wire [51:0] rom_1_data;

  and and_1 (and_1_out, COND2, ~COND1, COND0, INT);  // AND_Gate
  or or_1 (or_5_out[4], J4, and_1_out);
  and and_2 (and_2_out, COND2, ~COND1, ~COND0, PSR15);  // AND_Gate
  or or_2 (or_5_out[3], J3, and_2_out);
  Multiplexer #(.width(6)) multiplexer_1 (
    .in0({J5, or_5_out}), .in1({2'b00, IR15_11[4:1]}), .out(multiplexer_1_out), .sel(IRD));
  and and_3 (and_3_out, ~COND2, COND1, ~COND0, BEN);  // AND_Gate
  or or_3 (or_5_out[2], J2, and_3_out);
  Multiplexer #(.width(6)) multiplexer_2 (.in0(multiplexer_1_out), .in1(6'b010010), .out(NSN), .sel(RES));
  ROM #(.addrWidth(6), .dataWidth(52)) rom_1 (.addr(NSN), .data(rom_1_data));
  and and_4 (and_4_out, ~COND2, ~COND1, COND0, R);  // AND_Gate
  or or_4 (or_5_out[1], J1, and_4_out);
  and and_5 (and_5_out, ~COND2, COND1, COND0, IR15_11[0]);  // AND_Gate
  or or_5 (or_5_out[0], J0, and_5_out);
  Register #(.width(6)) CSNumber (.D(NSN), .en(1'b1), .Q(CSN), .clk(CLK), .clr(1'b0));
  Register #(.width(52)) register_1 (
    .D(rom_1_data), .en(1'b1), .clk(CLK),
    .Q({IRD, COND2, COND1, COND0, J5, J4, J3, J2, J1, J0, LDMAR, LDMDR, LDIR, LDBEN, LDREG, LDCC, LDPC, out_12[34:29], GatePC, GateMDR, GateALU, GateMARMUX, out_12[24:19], DRMUX, out_12[16:15], ADDR1MUX, ADDR2MUX, out_12[11:10], MARMUX, out_12[8:5], ALUK, MIOEN, out_12[1:0]}),
    .clr(1'b0));

  assign {out_12[41:35], out_12[28:25], out_12[18:17], out_12[14:12], out_12[9], out_12[4:2]} = {LDMAR, LDMDR, LDIR, LDBEN, LDREG, LDCC, LDPC, GatePC, GateMDR, GateALU, GateMARMUX, DRMUX, ADDR1MUX, ADDR2MUX, MARMUX, ALUK, MIOEN};
  assign PCMUX = out_12[20:19];
  assign RW = out_12[1];
  assign SR1MUX = out_12[16:15];
  assign SR2MUX = IR5;

  // Other names for the same wires on the sheet: IR15_12[3:0] = IR15_11[4:1]; IR11 = IR15_11[0]

  // Notes on the sheet:
  //   Interruption
  //   User Privilege Mode
  //   NEXT STATE NUMBER
  //   Branch
  //   contents of rom_1 (hex, n*v repeats v):
  //   2480000000000 483004008000 660002006200 5e0002006200 3500000000000 483004008008 660002009208
  //   5e0002009208 0 483004008010 62000200e208 76000200e208 480804108018 0 483002006200 720002000000
  //   1400000000006 0 5860810000000 0 4828100c8000 4828100c7000 480802106200 410004000018 1610000000004
  //   1650000000004 660008000000 483008000000 1712010040004 1750000000004 480808100000 5e0008000000
  //   8004000000000 1850000000004 0 808008000000
  //   Memory Ready
  //   Addressing Mode
  //   NEXT STATE
  //   CURRENT STATE
endmodule

module BEN_reg (
  input  D,
  input  LD,
  input  CLK,
  input  RESET,
  output Q
);

  Register #(.width(1)) register_1 (.D(D), .en(LD), .clk(CLK), .Q(Q), .clr(RESET));
endmodule

module memory (
  input  [15:0] ADDRESS,
  input  CLK,
  input  RES,
  input  [15:0] DATO,
  input  RW,
  input  MIOEN,
  output [15:0] MEM_OUT,
  output R
);

  wire and_1_out, and_2_out, not_1_out, or_1_out;

  not not_1 (not_1_out, RW);
  and and_1 (and_1_out, MIOEN, RW);
  and and_2 (and_2_out, MIOEN, not_1_out);
  RAM #(.addrWidth(16), .dataWidth(16)) ram_1 (
    .addr(ADDRESS), .we(and_1_out), .oe(and_2_out), .clk(CLK), .din(DATO), .dout(MEM_OUT));
  or or_1 (or_1_out, ~MIOEN, RES);  // OR_Gate
  Counter #(.max('h2), .width(2)) counter_1 (
    .count(MIOEN), .carry(R), .up(1'b1), .clk(CLK), .clr(or_1_out));  // open: load, D, Q
endmodule

module NZP_reg (
  input  P_IN,
  input  Z_IN,
  input  N_IN,
  input  LD,
  input  CLK,
  input  RESET,
  output N,
  output Z,
  output P
);

  Register #(.width(1)) register_1 (.D(N_IN), .en(LD), .clk(CLK), .Q(N), .clr(LD));
  Register #(.width(1)) register_2 (.D(Z_IN), .en(LD), .clk(CLK), .Q(Z), .clr(LD));
  Register #(.width(1)) register_3 (.D(P_IN), .en(LD), .clk(CLK), .Q(P), .clr(LD));

  assign RESET = LD;
endmodule
