// Logisim project Project_BK.circ as structural Verilog: 41 circuits, main circuit main
module BitComparator (
  input  A,
  input  B,
  input  E,
  input  G,
  output Gout,
  output Eout
);

  wire and_1_out, and_2_out, not_1_out, xnor_1_out;

  not not_1 (not_1_out, B);
  and and_1 (and_1_out, A, not_1_out);
  and and_2 (and_2_out, and_1_out, E);
  xnor xnor_1 (xnor_1_out, A, B);
  or or_1 (Gout, and_2_out, G);
  and and_3 (Eout, xnor_1_out, E);
endmodule

module main (
  input  INT_f,
  input  in_2,
  output [1:0] out_3,
  output [15:0] out_4,
  output [15:0] out_5,
  output [2:0] out_6,
  output [1:0] out_7,
  output [15:0] out_8,
  output [15:0] out_9,
  output [15:0] out_10,
  output [15:0] out_11,
  output [15:0] out_12,
  output [1:0] out_13,
  output [15:0] out_14,
  output [15:0] out_15,
  output [15:0] out_16,
  output [15:0] out_17,
  output out_18,
  output [15:0] out_19,
  output [15:0] out_20,
  output [15:0] out_21,
  output [15:0] out_22,
  output [15:0] out_23,
  output [15:0] out_24,
  output [15:0] out_25,
  output [15:0] out_26,
  output [15:0] out_27,
  output [15:0] out_28,
  output [15:0] out_29,
  output [15:0] out_30,
  output [15:0] out_31,
  output [15:0] out_32,
  output [15:0] out_33,
  output [15:0] out_34,
  output [15:0] out_35,
  output out_36,
  output out_37,
  output out_38,
  output [15:0] out_39,
  output [15:0] out_40,
  output out_41
);

  wire and_2_out, and_3_out, and_4_out, cl_out, CLK, d_ff_1_qn, GateALU, GateMARMUX, GateMDR, GatePC,
       GatePC_1, GatePSR, GateSP, GateVector, LDBEN, LDCC, LDIR, LDMAR, LDMDR, LDPC, LDPriority, LDPriv,
       LDREG, LDSavedSSP, LDSavedUSP, LDVector, logic_1_n, logic_1_p, logic_1_z, MARMUX, MIOEN, or_2_out,
       POWER_ON_out, R, RESET, RESET_out, RW, SetPriv, SR2MUX, t_ff_1_q, t_ff_2_q;
  wire [1:0] ALUK, SPMUX, SR1MUX, VectorMUX;
  wire [2:0] SR1_IN;
  wire [5:0] uc_1_csn, uc_1_nsn;
  wire [15:0] pc_mux_1_out_5, plus1_1_out_2, sext_5to16_1_out_2, sext_6to16_1_out_2, uc_1_out_11,
       zext_8to16_1_out_2;

  Button u_RESET (.out(RESET_out));
  Button POWER_ON (.out(POWER_ON_out));
  Clock cl (.out(cl_out));
  D_Flip_Flop d_ff_1 (.D(1'b1), .clk(CLK), .Qn(d_ff_1_qn), .reset(POWER_ON_out));  // open: Q, preset
  T_Flip_Flop t_ff_1 (.T(RESET_out), .clk(RESET_out), .Q(t_ff_1_q));  // open: Qn, reset, preset
  T_Flip_Flop t_ff_2 (.T(POWER_ON_out), .clk(POWER_ON_out), .Q(t_ff_2_q));  // open: Qn, reset, preset
  or or_1 (RESET, d_ff_1_qn, t_ff_1_q);
  and and_1 (CLK, t_ff_2_q, cl_out);
  assign out_20 = GateMARMUX ? out_5 : 16'bz;  // Controlled_Buffer controlled_buffer_1
  mar_mux mar_mux_1 (.Control(MARMUX), .In1(zext_8to16_1_out_2), .In2(out_8), .mux_out(out_5));
  ZEXT_8to16 zext_8to16_1 (.in_1(out_19[7:0]), .out_2(zext_8to16_1_out_2));
  assign out_20 = GateMDR ? out_21 : 16'bz;  // Controlled_Buffer controlled_buffer_2
  MDR_reg mdr_reg_1 (.LD_MDR(LDMDR), .CLK(CLK), .RES(RESET), .MDR_IN(out_24), .MDR_OUT(out_21));
  mux2x1_16Bits mux2x1_16bits_1 (.in_2(out_20), .in_3(out_25), .in_1(MIOEN), .out_4(out_24));
  SEXT_11to16 sext_11to16_1 (.in_1(out_19[10:0]), .out_2(out_14));
  SEXT_9to16 sext_9to16_1 (.in_1(out_19[8:0]), .out_2(out_17));
  SEXT_6to16 sext_6to16_1 (.in_1(out_19[5:0]), .out_2(sext_6to16_1_out_2));
  IR_Register ir_register_1 (.LD_IR(LDIR), .CLK(CLK), .RES(RESET), .IR_IN(out_20), .IR_OUT(out_19));
  memory memory_1 (
    .MEMEN(1'b1), .ADDRESS(out_23), .DATO(out_21), .CLK(CLK), .RES(RESET), .RW(RW), .MIOEN(MIOEN), .R(R),
    .MEM_OUT(out_25));
  addr2_mux addr2_mux_1 (
    .In1({16{1'b0}}), .In2(sext_6to16_1_out_2), .In3(out_17), .In4(out_14), .in_1(out_13), .out_6(out_11));
  fullAdder fulladder_1 (.A(out_12), .B(out_11), .R(out_8));
  MAR_reg mar_reg_1 (.LD_MAR(LDMAR), .CLK(CLK), .RES(RESET), .MAR_IN(out_20), .MAR_OUT(out_23));
  and and_2 (and_2_out, out_19[11], out_36);
  and and_3 (and_3_out, out_19[10], out_37);
  and and_4 (and_4_out, out_19[9], out_38);
  mux2x1_16Bits mux2x1_16bits_2 (.in_2(out_10), .in_3(out_4), .in_1(out_13[1]), .out_4(out_12));
  or or_2 (or_2_out, and_2_out, and_3_out, and_4_out);
  NZP_reg nzp_reg_1 (
    .P_IN(logic_1_p), .Z_IN(logic_1_z), .N_IN(logic_1_n), .LD(LDCC), .CLK(CLK), .RESET(RESET), .N(out_36),
    .Z(out_37), .P(out_38));
  \logic  logic_1 (.in_1(out_20), .P(logic_1_p), .Z(logic_1_z), .N(logic_1_n));
  assign out_20 = GatePC ? out_4 : 16'bz;  // Controlled_Buffer controlled_buffer_3
  PC_reg pc_reg_1 (.CLK(CLK), .LDPC(LDPC), .RES(RESET), .DIN(pc_mux_1_out_5), .out_5(out_4));
  PC_mux pc_mux_1 (.Control(out_7), .In1(plus1_1_out_2), .In2(out_8), .In3(out_20), .out_5(pc_mux_1_out_5));
  BEN_reg ben_reg_1 (.D(or_2_out), .LD(LDBEN), .CLK(CLK), .RESET(RESET), .Q(out_18));
  SEXT_5to16 sext_5to16_1 (.in_1(out_19[4:0]), .out_2(sext_5to16_1_out_2));
  // Probe on {LDMAR, LDMDR, LDIR, LDBEN, LDREG, LDCC, LDPC, LDPriv, LDSavedSSP, LDSavedUSP, LDVector, LDPriority, GatePC, GateMDR, GateALU, GateMARMUX, GateVector, GatePC_1, GatePSR, GateSP, out_7, out_3, SR1MUX, uc_1_out_11[15], out_13, SPMUX, MARMUX, VectorMUX, uc_1_out_11[7], ALUK, MIOEN, RW, SetPriv, SR2MUX, uc_1_out_11[0]}
  // Probe on uc_1_nsn
  // Probe on uc_1_csn
  UC uc_1 (
    .IR5(out_19[5]), .INT(INT_f), .R(R), .BEN(out_18), .PSR15(in_2), .IR15_11(out_19[15:11]), .CLK(CLK),
    .RES(RESET), .NSN(uc_1_nsn), .CSN(uc_1_csn),
    .out_11({LDMAR, LDMDR, LDIR, LDBEN, LDREG, LDCC, LDPC, LDPriv, LDSavedSSP, LDSavedUSP, LDVector, LDPriority, GatePC, GateMDR, GateALU, GateMARMUX, GateVector, GatePC_1, GatePSR, GateSP, out_7, out_3, SR1MUX, uc_1_out_11[15], out_13, SPMUX, MARMUX, VectorMUX, uc_1_out_11[7], ALUK, MIOEN, RW, SetPriv, SR2MUX, uc_1_out_11[0]}));
  plus1 plus1_1 (.in_1(out_4), .out_2(plus1_1_out_2));
  // NoConnect on uc_1_out_11[0]
  Multiplexer #(.select(2), .width(3)) multiplexer_1 (
    .in0(out_19[11:9]), .in1(3'b110), .in2(3'b111), .out(out_6), .sel(out_3));  // open: in3
  Multiplexer #(.select(2), .width(3)) multiplexer_2 (
    .in0(out_19[11:9]), .in1(out_19[8:6]), .in2(3'b110), .out(SR1_IN), .sel(SR1MUX));  // open: in3
  SR2_mux sr2_mux_1 (.Control(SR2MUX), .In1(out_9), .In2(sext_5to16_1_out_2), .mux_out(out_15));
  fileRegister fileregister_1 (
    .DR(out_6), .LDREG(LDREG), .CLK(CLK), .RES(RESET), .SR1(SR1_IN), .SR2(out_19[2:0]), .DIN(out_20),
    .R3(out_29), .R4(out_30), .R5(out_31), .R0(out_26), .R6(out_32), .R7(out_33), .R1(out_27), .R2(out_28),
    .SR1OUT(out_10), .SR2OUT(out_9));
  ALU alu_1 (.Selector(ALUK), .A(out_10), .B(out_15), .Result(out_16));
  assign out_20 = GateALU ? out_16 : 16'bz;  // Controlled_Buffer controlled_buffer_4

  assign out_22 = out_20;
  assign out_34 = out_23;
  assign out_35 = out_21;
  assign out_39 = out_19;
  assign out_40 = out_4;
  assign out_41 = out_18;

  // Other names for the same wires on the sheet: ADDR2MUX[1:0] = out_13; ADDR1MUX = out_13[1]; BEN = out_18;
  //   DRMUX[1:0] = out_3; INT = INT_f; IR[15:0] = out_19; MAR[15:0] = out_23; MDR[15:0] = out_21; N = out_36;
  //   P = out_38; PC[15:0] = out_4; PCMUX[1:0] = out_7; PSR15 = in_2; R0[15:0] = out_26; R1[15:0] = out_27;
  //   R2[15:0] = out_28; R3[15:0] = out_29; R4[15:0] = out_30; R5[15:0] = out_31; R6[15:0] = out_32;
  //   R7[15:0] = out_33; Z = out_37
endmodule

module AND16 (
  input  in_1,
  input  in_2,
  input  in_3,
  input  in_4,
  input  in_5,
  input  in_6,
  input  in_7,
  input  in_8,
  input  in_9,
  input  in_10,
  input  in_11,
  input  in_12,
  input  in_13,
  input  in_14,
  input  in_15,
  input  in_16,
  output out_17
);

  wire and_1_out, and_2_out, and_3_out, and_4_out, and_5_out, and_6_out, and_7_out, and_8_out, and_9_out,
       and_10_out, and_11_out, and_12_out, and_13_out, and_14_out;

  and and_1 (and_1_out, in_15, in_16);
  and and_2 (and_2_out, in_14, and_1_out);
  and and_3 (and_3_out, in_13, and_2_out);
  and and_4 (and_4_out, in_12, and_3_out);
  and and_5 (and_5_out, in_11, and_4_out);
  and and_6 (and_6_out, in_9, and_7_out);
  and and_7 (and_7_out, in_10, and_5_out);
  and and_8 (and_8_out, in_8, and_6_out);
  and and_9 (and_9_out, in_7, and_8_out);
  and and_10 (and_10_out, in_6, and_9_out);
  and and_11 (and_11_out, in_5, and_10_out);
  and and_12 (and_12_out, in_3, and_13_out);
  and and_13 (and_13_out, in_4, and_11_out);
  and and_14 (and_14_out, in_2, and_12_out);
  and and_15 (out_17, in_1, and_14_out);
endmodule

module Comparator16Bit (
  input  [15:0] A,
  input  [15:0] B,
  output Great,
  output Equal,
  output Less
);

  wire bitcomparator_1_eout, bitcomparator_1_gout, bitcomparator_2_eout, bitcomparator_2_gout,
       bitcomparator_3_eout, bitcomparator_3_gout, bitcomparator_4_eout, bitcomparator_4_gout,
       bitcomparator_5_eout, bitcomparator_5_gout, bitcomparator_6_eout, bitcomparator_6_gout,
       bitcomparator_7_eout, bitcomparator_7_gout, bitcomparator_8_eout, bitcomparator_8_gout,
       bitcomparator_9_eout, bitcomparator_9_gout, bitcomparator_10_eout, bitcomparator_10_gout,
       bitcomparator_11_eout, bitcomparator_11_gout, bitcomparator_12_eout, bitcomparator_12_gout,
       bitcomparator_13_eout, bitcomparator_13_gout, bitcomparator_14_eout, bitcomparator_14_gout,
       bitcomparator_15_eout, bitcomparator_15_gout, bitcomparator_16_eout, bitcomparator_16_gout, not_1_out,
       xor_1_out;

  BitComparator bitcomparator_1 (
    .A(A[0]), .B(B[0]), .E(bitcomparator_2_eout), .G(bitcomparator_2_gout), .Gout(bitcomparator_1_gout),
    .Eout(bitcomparator_1_eout));
  BitComparator bitcomparator_2 (
    .A(A[1]), .B(B[1]), .E(bitcomparator_3_eout), .G(bitcomparator_3_gout), .Gout(bitcomparator_2_gout),
    .Eout(bitcomparator_2_eout));
  BitComparator bitcomparator_3 (
    .A(A[2]), .B(B[2]), .E(bitcomparator_4_eout), .G(bitcomparator_4_gout), .Gout(bitcomparator_3_gout),
    .Eout(bitcomparator_3_eout));
  BitComparator bitcomparator_4 (
    .A(A[3]), .B(B[3]), .E(bitcomparator_5_eout), .G(bitcomparator_5_gout), .Gout(bitcomparator_4_gout),
    .Eout(bitcomparator_4_eout));
  BitComparator bitcomparator_5 (
    .A(A[4]), .B(B[4]), .E(bitcomparator_6_eout), .G(bitcomparator_6_gout), .Gout(bitcomparator_5_gout),
    .Eout(bitcomparator_5_eout));
  BitComparator bitcomparator_6 (
    .A(A[5]), .B(B[5]), .E(bitcomparator_7_eout), .G(bitcomparator_7_gout), .Gout(bitcomparator_6_gout),
    .Eout(bitcomparator_6_eout));
  BitComparator bitcomparator_7 (
    .A(A[6]), .B(B[6]), .E(bitcomparator_8_eout), .G(bitcomparator_8_gout), .Gout(bitcomparator_7_gout),
    .Eout(bitcomparator_7_eout));
  BitComparator bitcomparator_8 (
    .A(A[7]), .B(B[7]), .E(bitcomparator_9_eout), .G(bitcomparator_9_gout), .Gout(bitcomparator_8_gout),
    .Eout(bitcomparator_8_eout));
  BitComparator bitcomparator_9 (
    .A(A[8]), .B(B[8]), .E(bitcomparator_10_eout), .G(bitcomparator_10_gout), .Gout(bitcomparator_9_gout),
    .Eout(bitcomparator_9_eout));
  BitComparator bitcomparator_10 (
    .A(A[9]), .B(B[9]), .E(bitcomparator_11_eout), .G(bitcomparator_11_gout), .Gout(bitcomparator_10_gout),
    .Eout(bitcomparator_10_eout));
  BitComparator bitcomparator_11 (
    .A(A[10]), .B(B[10]), .E(bitcomparator_12_eout), .G(bitcomparator_12_gout), .Gout(bitcomparator_11_gout),
    .Eout(bitcomparator_11_eout));
  BitComparator bitcomparator_12 (
    .A(A[11]), .B(B[11]), .E(bitcomparator_13_eout), .G(bitcomparator_13_gout), .Gout(bitcomparator_12_gout),
    .Eout(bitcomparator_12_eout));
  BitComparator bitcomparator_13 (
    .A(A[12]), .B(B[12]), .E(bitcomparator_14_eout), .G(bitcomparator_14_gout), .Gout(bitcomparator_13_gout),
    .Eout(bitcomparator_13_eout));
  BitComparator bitcomparator_14 (
    .A(A[13]), .B(B[13]), .E(bitcomparator_15_eout), .G(bitcomparator_15_gout), .Gout(bitcomparator_14_gout),
    .Eout(bitcomparator_14_eout));
  BitComparator bitcomparator_15 (
    .A(A[14]), .B(B[14]), .E(bitcomparator_16_eout), .G(bitcomparator_16_gout), .Gout(bitcomparator_15_gout),
    .Eout(bitcomparator_15_eout));
  BitComparator bitcomparator_16 (
    .A(A[15]), .B(B[15]), .E(1'b1), .G(1'b0), .Gout(bitcomparator_16_gout), .Eout(bitcomparator_16_eout));
  not not_1 (not_1_out, bitcomparator_1_gout);
  xor xor_1 (xor_1_out, A[15], B[15]);
  Multiplexer multiplexer_1 (.in0(bitcomparator_1_gout), .in1(not_1_out), .out(Great), .sel(xor_1_out));
  AND16 and16_1 (
    .in_1(bitcomparator_1_eout), .in_2(bitcomparator_2_eout), .in_3(bitcomparator_3_eout),
    .in_4(bitcomparator_4_eout), .in_5(bitcomparator_5_eout), .in_6(bitcomparator_6_eout),
    .in_7(bitcomparator_7_eout), .in_8(bitcomparator_8_eout), .in_9(bitcomparator_9_eout),
    .in_10(bitcomparator_10_eout), .in_11(bitcomparator_11_eout), .in_12(bitcomparator_12_eout),
    .in_13(bitcomparator_13_eout), .in_14(bitcomparator_14_eout), .in_15(bitcomparator_15_eout),
    .in_16(bitcomparator_16_eout), .out_17(Equal));
  nor nor_1 (Less, Great, Equal);
endmodule

module ALU_Taller (
  input  [15:0] A,
  input  [15:0] B,
  input  [2:0] Selector,
  output P,
  output Z,
  output N,
  output [15:0] Result,
  output Overflow
);

  wire adder16bits_1_c_out, adder16bits_1_penult_carry_out, comparator16bit_1_equal, or_1_out,
       subs16bits_1_cout, subs16bits_1_pcarry, xor_1_out, xor_2_out;
  wire [15:0] adder16bits_1_sum, and16bitwise_1_r, not16bitwise_1_r, not16bitwise_2_r, or16bitwise_1_r,
       subs16bits_1_r;

  Adder16Bits adder16bits_1 (
    .A(A), .B(B), .C_Out(adder16bits_1_c_out), .penult_carry_out(adder16bits_1_penult_carry_out),
    .Sum(adder16bits_1_sum));
  xor xor_1 (xor_1_out, adder16bits_1_c_out, adder16bits_1_penult_carry_out);
  subs16Bits subs16bits_1 (.A(A), .B(B), .R(subs16bits_1_r), .Cout(subs16bits_1_cout), .Pcarry(subs16bits_1_pcarry));
  xor xor_2 (xor_2_out, subs16bits_1_pcarry, subs16bits_1_cout);
  or or_1 (or_1_out, xor_2_out, comparator16bit_1_equal);
  AND16Bitwise and16bitwise_1 (.A(A), .B(B), .R(and16bitwise_1_r));
  mux8x1 mux8x1_1 (
    .S(Selector), .A(xor_1_out), .B(or_1_out), .C(1'b0), .D(1'b0), .E(1'b0), .F(1'b0), .G(1'b0), .H(1'b0),
    .o(Overflow));
  OR16Bitwise or16bitwise_1 (.A(A), .B(B), .R(or16bitwise_1_r));
  Multiplexer #(.select(3), .width(16)) multiplexer_1 (
    .in0(adder16bits_1_sum), .in1(subs16bits_1_r), .in2(and16bitwise_1_r), .in3(or16bitwise_1_r),
    .in4(not16bitwise_1_r), .in5(not16bitwise_2_r), .in6(A), .in7(B), .out(Result), .sel(Selector));
  Comparator16Bit comparator16bit_1 (.A(B), .B(16'h8000), .Equal(comparator16bit_1_equal));  // open: Less, Great
  NOT16Bitwise not16bitwise_1 (.A(A), .R(not16bitwise_1_r));
  Comparator16Bit comparator16bit_2 (.A(Result), .B({16{1'b0}}), .Less(N), .Great(P), .Equal(Z));
  NOT16Bitwise not16bitwise_2 (.A(B), .R(not16bitwise_2_r));

  // Notes on the sheet:
  //   0 : Suma
  //   1 : Resta
  //   2 :AND Bitwise
  //   3 :OR Bitwise
  //   4 :NOT A
  //   5 :NOT B
  //   6: A
  //   7: B
endmodule

module bitAdd (
  input  A,
  input  B,
  input  CarryIn,
  output Sum,
  output CarryOut
);

  wire and_1_out, and_2_out, xor_1_out;

  xor xor_1 (xor_1_out, A, B);
  and and_1 (and_1_out, xor_1_out, CarryIn);
  and and_2 (and_2_out, A, B);
  xor xor_2 (Sum, xor_1_out, CarryIn);
  or or_1 (CarryOut, and_1_out, and_2_out);
endmodule

module Adder16Bits (
  input  [15:0] A,
  input  [15:0] B,
  output C_Out,
  output penult_carry_out,
  output [15:0] Sum
);

  wire N00_carryout, N01_carryout, N02_carryout, N03_carryout, N04_carryout, N05_carryout, N06_carryout,
       N07_carryout, N08_carryout, N09_carryout, N10_carryout, N11_carryout, N12_carryout, N13_carryout;

  bitAdd N15 (.B(A[15]), .CarryIn(penult_carry_out), .A(B[15]), .Sum(Sum[15]), .CarryOut(C_Out));
  bitAdd N14 (.B(A[14]), .CarryIn(N13_carryout), .A(B[14]), .Sum(Sum[14]), .CarryOut(penult_carry_out));
  bitAdd N13 (.B(A[13]), .CarryIn(N12_carryout), .A(B[13]), .Sum(Sum[13]), .CarryOut(N13_carryout));
  bitAdd N12 (.B(A[12]), .CarryIn(N11_carryout), .A(B[12]), .Sum(Sum[12]), .CarryOut(N12_carryout));
  bitAdd N11 (.B(A[11]), .CarryIn(N10_carryout), .A(B[11]), .Sum(Sum[11]), .CarryOut(N11_carryout));
  bitAdd N10 (.B(A[10]), .CarryIn(N09_carryout), .A(B[10]), .Sum(Sum[10]), .CarryOut(N10_carryout));
  bitAdd N09 (.B(A[9]), .CarryIn(N08_carryout), .A(B[9]), .Sum(Sum[9]), .CarryOut(N09_carryout));
  bitAdd N08 (.B(A[8]), .CarryIn(N07_carryout), .A(B[8]), .Sum(Sum[8]), .CarryOut(N08_carryout));
  bitAdd N07 (.B(A[7]), .CarryIn(N06_carryout), .A(B[7]), .Sum(Sum[7]), .CarryOut(N07_carryout));
  bitAdd N06 (.B(A[6]), .CarryIn(N05_carryout), .A(B[6]), .Sum(Sum[6]), .CarryOut(N06_carryout));
  bitAdd N05 (.B(A[5]), .CarryIn(N04_carryout), .A(B[5]), .Sum(Sum[5]), .CarryOut(N05_carryout));
  bitAdd N04 (.B(A[4]), .CarryIn(N03_carryout), .A(B[4]), .Sum(Sum[4]), .CarryOut(N04_carryout));
  bitAdd N03 (.B(A[3]), .CarryIn(N02_carryout), .A(B[3]), .Sum(Sum[3]), .CarryOut(N03_carryout));
  bitAdd N02 (.B(A[2]), .CarryIn(N01_carryout), .A(B[2]), .Sum(Sum[2]), .CarryOut(N02_carryout));
  bitAdd N01 (.B(A[1]), .CarryIn(N00_carryout), .A(B[1]), .Sum(Sum[1]), .CarryOut(N01_carryout));
  bitAdd N00 (.B(A[0]), .A(B[0]), .Sum(Sum[0]), .CarryOut(N00_carryout));  // open: CarryIn
endmodule

module AND16Bitwise (
  input  [15:0] A,
  input  [15:0] B,
  output [15:0] R
);

  and and_1 (R[15], B[15], A[15]);
  and and_2 (R[14], B[14], A[14]);
  and and_3 (R[13], B[13], A[13]);
  and and_4 (R[12], B[12], A[12]);
  and and_5 (R[11], B[11], A[11]);
  and and_6 (R[10], B[10], A[10]);
  and and_7 (R[9], B[9], A[9]);
  and and_8 (R[8], B[8], A[8]);
  and and_9 (R[7], B[7], A[7]);
  and and_10 (R[6], B[6], A[6]);
  and and_11 (R[5], B[5], A[5]);
  and and_12 (R[4], B[4], A[4]);
  and and_13 (R[3], B[3], A[3]);
  and and_14 (R[2], B[2], A[2]);
  and and_15 (R[1], B[1], A[1]);
  and and_16 (R[0], B[0], A[0]);
endmodule

module OR16Bitwise (
  input  [15:0] A,
  input  [15:0] B,
  output [15:0] R
);

  or or_1 (R[15], B[15], A[15]);
  or or_2 (R[14], B[14], A[14]);
  or or_3 (R[13], B[13], A[13]);
  or or_4 (R[12], B[12], A[12]);
  or or_5 (R[11], B[11], A[11]);
  or or_6 (R[10], B[10], A[10]);
  or or_7 (R[9], B[9], A[9]);
  or or_8 (R[8], B[8], A[8]);
  or or_9 (R[7], B[7], A[7]);
  or or_10 (R[6], B[6], A[6]);
  or or_11 (R[5], B[5], A[5]);
  or or_12 (R[4], B[4], A[4]);
  or or_13 (R[3], B[3], A[3]);
  or or_14 (R[2], B[2], A[2]);
  or or_15 (R[1], B[1], A[1]);
  or or_16 (R[0], B[0], A[0]);
endmodule

module XOR16Bitwise (
  input  [15:0] A,
  input  [15:0] B,
  output [15:0] R
);

  xor xor_1 (R[15], B[15], A[15]);
  xor xor_2 (R[14], B[14], A[14]);
  xor xor_3 (R[13], B[13], A[13]);
  xor xor_4 (R[12], B[12], A[12]);
  xor xor_5 (R[11], B[11], A[11]);
  xor xor_6 (R[10], B[10], A[10]);
  xor xor_7 (R[9], B[9], A[9]);
  xor xor_8 (R[8], B[8], A[8]);
  xor xor_9 (R[7], B[7], A[7]);
  xor xor_10 (R[6], B[6], A[6]);
  xor xor_11 (R[5], B[5], A[5]);
  xor xor_12 (R[4], B[4], A[4]);
  xor xor_13 (R[3], B[3], A[3]);
  xor xor_14 (R[2], B[2], A[2]);
  xor xor_15 (R[1], B[1], A[1]);
  xor xor_16 (R[0], B[0], A[0]);
endmodule

module NOT16Bitwise (
  input  [15:0] A,
  output [15:0] R
);

  not not_1 (R[15], A[15]);
  not not_2 (R[14], A[14]);
  not not_3 (R[13], A[13]);
  not not_4 (R[12], A[12]);
  not not_5 (R[11], A[11]);
  not not_6 (R[10], A[10]);
  not not_7 (R[9], A[9]);
  not not_8 (R[8], A[8]);
  not not_9 (R[7], A[7]);
  not not_10 (R[6], A[6]);
  not not_11 (R[5], A[5]);
  not not_12 (R[4], A[4]);
  not not_13 (R[3], A[3]);
  not not_14 (R[2], A[2]);
  not not_15 (R[1], A[1]);
  not not_16 (R[0], A[0]);
endmodule

module subs16Bits (
  input  [15:0] A,
  input  [15:0] B,
  output Cout,
  output Pcarry,
  output [15:0] R
);

  wire [15:0] adder16bits_2_sum, xor16bitwise_1_r;

  Adder16Bits adder16bits_1 (.A(A), .B(adder16bits_2_sum), .C_Out(Cout), .penult_carry_out(Pcarry), .Sum(R));
  Adder16Bits adder16bits_2 (
    .A(16'h1), .B(xor16bitwise_1_r), .Sum(adder16bits_2_sum));  // open: C_Out, penult_carry_out
  XOR16Bitwise xor16bitwise_1 (.A({16{1'b1}}), .B(B), .R(xor16bitwise_1_r));
endmodule

module mux2x1 (
  input  A,
  input  B,
  input  S,
  output out_4
);

  wire and_1_out, and_2_out, not_1_out;

  not not_1 (not_1_out, S);
  and and_1 (and_1_out, A, not_1_out);
  and and_2 (and_2_out, B, S);
  or or_1 (out_4, and_1_out, and_2_out);
endmodule

module mux8x1 (
  input  A,
  input  B,
  input  C,
  input  D,
  input  E,
  input  F,
  input  G,
  input  H,
  input  [2:0] S,
  output o
);

  wire and_1_out, and_2_out, and_3_out, and_4_out, and_5_out, and_6_out, and_7_out, and_8_out, and_9_out,
       and_10_out, and_11_out, and_12_out, and_13_out, and_14_out, and_15_out, and_16_out, and_17_out,
       and_18_out, and_19_out, and_20_out, and_21_out, and_22_out, and_23_out, and_24_out, not_1_out,
       not_2_out, not_3_out, not_4_out, not_5_out, not_6_out, not_7_out, not_8_out, not_9_out, not_10_out,
       not_11_out, not_12_out, or_1_out, or_2_out, or_3_out, or_4_out, or_5_out, or_6_out;

  not not_1 (not_1_out, S[0]);
  not not_2 (not_2_out, S[0]);
  not not_3 (not_3_out, S[0]);
  not not_4 (not_4_out, S[0]);
  and and_1 (and_1_out, A, not_1_out);
  not not_5 (not_5_out, S[1]);
  and and_2 (and_2_out, B, S[0]);
  not not_6 (not_6_out, S[1]);
  and and_3 (and_3_out, C, not_2_out);
  and and_4 (and_4_out, D, S[0]);
  and and_5 (and_5_out, E, not_3_out);
  not not_7 (not_7_out, S[1]);
  and and_6 (and_6_out, F, S[0]);
  not not_8 (not_8_out, S[1]);
  and and_7 (and_7_out, G, not_4_out);
  and and_8 (and_8_out, H, S[0]);
  and and_9 (and_9_out, and_1_out, not_5_out);
  and and_10 (and_10_out, and_2_out, not_6_out);
  and and_11 (and_11_out, and_3_out, S[1]);
  and and_12 (and_12_out, and_4_out, S[1]);
  and and_13 (and_13_out, and_5_out, not_7_out);
  and and_14 (and_14_out, and_6_out, not_8_out);
  and and_15 (and_15_out, and_7_out, S[1]);
  and and_16 (and_16_out, and_8_out, S[1]);
  and and_17 (and_17_out, and_9_out, not_9_out);
  not not_9 (not_9_out, S[2]);
  and and_18 (and_18_out, and_10_out, not_10_out);
  not not_10 (not_10_out, S[2]);
  and and_19 (and_19_out, and_11_out, not_11_out);
  not not_11 (not_11_out, S[2]);
  and and_20 (and_20_out, and_12_out, not_12_out);
  not not_12 (not_12_out, S[2]);
  and and_21 (and_21_out, and_13_out, S[2]);
  buf and_22 (and_22_out, and_14_out);  // AND_Gate
  and and_23 (and_23_out, and_15_out, S[2]);
  and and_24 (and_24_out, and_16_out, S[2]);
  or or_1 (or_1_out, and_17_out, and_18_out);
  or or_2 (or_2_out, and_19_out, and_20_out);
  or or_3 (or_3_out, and_21_out, and_22_out);
  or or_4 (or_4_out, and_23_out, and_24_out);
  or or_5 (or_5_out, or_1_out, or_2_out);
  or or_6 (or_6_out, or_3_out, or_4_out);
  or or_7 (o, or_5_out, or_6_out);
endmodule

module testComparator (
  input  [15:0] in_1,
  input  [15:0] in_2,
  input  [15:0] in_3,
  input  [15:0] in_4,
  input  [15:0] in_5,
  input  [15:0] in_6,
  input  [15:0] in_7,
  input  [15:0] in_8,
  output out_9,
  output out_10,
  output out_11,
  output out_12,
  output out_13,
  output out_14,
  output out_15,
  output out_16,
  output out_17,
  output out_18,
  output out_19,
  output out_20
);

  Comparator16Bit comparator16bit_1 (.A(in_1), .B(in_3), .Less(out_13), .Great(out_9), .Equal(out_11));
  Comparator16Bit comparator16bit_2 (.A(in_6), .B(in_8), .Less(out_20), .Great(out_16), .Equal(out_18));
  Comparator16Bit comparator16bit_3 (.A(in_2), .B(in_4), .Less(out_14), .Great(out_10), .Equal(out_12));
  Comparator16Bit comparator16bit_4 (.A(in_5), .B(in_7), .Less(out_19), .Great(out_15), .Equal(out_17));
endmodule

module PriotyEncoder4to2 (
  input  I0,
  input  I1,
  input  I2,
  input  I3,
  output V,
  output Y0,
  output Y1
);

  wire and_1_out, not_1_out;

  not not_1 (not_1_out, I2);
  and and_1 (and_1_out, I1, not_1_out);
  or or_1 (V, I0, I1, I2, I3);
  or or_2 (Y0, and_1_out, I3);
  or or_3 (Y1, I2, I3);
endmodule

module mux4x1 (
  input  in_1,
  input  in_2,
  input  in_3,
  input  in_4,
  input  [1:0] in_5,
  output out_6
);

  wire and_1_out, and_2_out, and_3_out, and_4_out, and_5_out, and_6_out, and_7_out, and_8_out, not_1_out,
       not_2_out, not_3_out, not_4_out, or_1_out, or_2_out;

  not not_1 (not_1_out, in_5[0]);
  not not_2 (not_2_out, in_5[0]);
  and and_1 (and_1_out, in_1, not_1_out);
  and and_2 (and_2_out, in_2, in_5[0]);
  and and_3 (and_3_out, in_3, not_2_out);
  and and_4 (and_4_out, in_4, in_5[0]);
  not not_3 (not_3_out, in_5[1]);
  not not_4 (not_4_out, in_5[1]);
  and and_5 (and_5_out, and_1_out, not_3_out);
  and and_6 (and_6_out, and_2_out, not_4_out);
  and and_7 (and_7_out, and_3_out, in_5[1]);
  and and_8 (and_8_out, and_4_out, in_5[1]);
  or or_1 (or_1_out, and_5_out, and_6_out);
  or or_2 (or_2_out, and_7_out, and_8_out);
  or or_3 (out_6, or_1_out, or_2_out);
endmodule

module mux4x1_16Bits (
  input  [1:0] in_1,
  input  [15:0] in_2,
  input  [15:0] in_3,
  input  [15:0] in_4,
  input  [15:0] in_5,
  output [15:0] out_6
);

  mux4x1 mux4x1_1 (.in_1(in_2[0]), .in_2(in_3[0]), .in_3(in_4[0]), .in_4(in_5[0]), .in_5(in_1), .out_6(out_6[0]));
  mux4x1 mux4x1_2 (.in_1(in_2[1]), .in_2(in_3[1]), .in_3(in_4[1]), .in_4(in_5[1]), .in_5(in_1), .out_6(out_6[1]));
  mux4x1 mux4x1_3 (.in_1(in_2[2]), .in_2(in_3[2]), .in_3(in_4[2]), .in_4(in_5[2]), .in_5(in_1), .out_6(out_6[2]));
  mux4x1 mux4x1_4 (.in_1(in_2[3]), .in_2(in_3[3]), .in_3(in_4[3]), .in_4(in_5[3]), .in_5(in_1), .out_6(out_6[3]));
  mux4x1 mux4x1_5 (.in_1(in_2[4]), .in_2(in_3[4]), .in_3(in_4[4]), .in_4(in_5[4]), .in_5(in_1), .out_6(out_6[4]));
  mux4x1 mux4x1_6 (.in_1(in_2[5]), .in_2(in_3[5]), .in_3(in_4[5]), .in_4(in_5[5]), .in_5(in_1), .out_6(out_6[5]));
  mux4x1 mux4x1_7 (.in_1(in_2[6]), .in_2(in_3[6]), .in_3(in_4[6]), .in_4(in_5[6]), .in_5(in_1), .out_6(out_6[6]));
  mux4x1 mux4x1_8 (.in_1(in_2[7]), .in_2(in_3[7]), .in_3(in_4[7]), .in_4(in_5[7]), .in_5(in_1), .out_6(out_6[7]));
  mux4x1 mux4x1_9 (.in_1(in_2[8]), .in_2(in_3[8]), .in_3(in_4[8]), .in_4(in_5[8]), .in_5(in_1), .out_6(out_6[8]));
  mux4x1 mux4x1_10 (.in_1(in_2[9]), .in_2(in_3[9]), .in_3(in_4[9]), .in_4(in_5[9]), .in_5(in_1), .out_6(out_6[9]));
  mux4x1 mux4x1_11 (.in_1(in_2[10]), .in_2(in_3[10]), .in_3(in_4[10]), .in_4(in_5[10]), .in_5(in_1), .out_6(out_6[10]));
  mux4x1 mux4x1_12 (.in_1(in_2[11]), .in_2(in_3[11]), .in_3(in_4[11]), .in_4(in_5[11]), .in_5(in_1), .out_6(out_6[11]));
  mux4x1 mux4x1_13 (.in_1(in_2[12]), .in_2(in_3[12]), .in_3(in_4[12]), .in_4(in_5[12]), .in_5(in_1), .out_6(out_6[12]));
  mux4x1 mux4x1_14 (.in_1(in_2[13]), .in_2(in_3[13]), .in_3(in_4[13]), .in_4(in_5[13]), .in_5(in_1), .out_6(out_6[13]));
  mux4x1 mux4x1_15 (.in_1(in_2[14]), .in_2(in_3[14]), .in_3(in_4[14]), .in_4(in_5[14]), .in_5(in_1), .out_6(out_6[14]));
  mux4x1 mux4x1_16 (.in_1(in_2[15]), .in_2(in_3[15]), .in_3(in_4[15]), .in_4(in_5[15]), .in_5(in_1), .out_6(out_6[15]));
endmodule

module mux2x1_16Bits (
  input  in_1,
  input  [15:0] in_2,
  input  [15:0] in_3,
  output [15:0] out_4
);

  mux2x1 mux2x1_1 (.A(in_2[0]), .B(in_3[0]), .S(in_1), .out_4(out_4[0]));
  mux2x1 mux2x1_2 (.A(in_2[1]), .B(in_3[1]), .S(in_1), .out_4(out_4[1]));
  mux2x1 mux2x1_3 (.A(in_2[2]), .B(in_3[2]), .S(in_1), .out_4(out_4[2]));
  mux2x1 mux2x1_4 (.A(in_2[3]), .B(in_3[3]), .S(in_1), .out_4(out_4[3]));
  mux2x1 mux2x1_5 (.A(in_2[4]), .B(in_3[4]), .S(in_1), .out_4(out_4[4]));
  mux2x1 mux2x1_6 (.A(in_2[5]), .B(in_3[5]), .S(in_1), .out_4(out_4[5]));
  mux2x1 mux2x1_7 (.A(in_2[6]), .B(in_3[6]), .S(in_1), .out_4(out_4[6]));
  mux2x1 mux2x1_8 (.A(in_2[7]), .B(in_3[7]), .S(in_1), .out_4(out_4[7]));
  mux2x1 mux2x1_9 (.A(in_2[8]), .B(in_3[8]), .S(in_1), .out_4(out_4[8]));
  mux2x1 mux2x1_10 (.A(in_2[9]), .B(in_3[9]), .S(in_1), .out_4(out_4[9]));
  mux2x1 mux2x1_11 (.A(in_2[10]), .B(in_3[10]), .S(in_1), .out_4(out_4[10]));
  mux2x1 mux2x1_12 (.A(in_2[11]), .B(in_3[11]), .S(in_1), .out_4(out_4[11]));
  mux2x1 mux2x1_13 (.A(in_2[12]), .B(in_3[12]), .S(in_1), .out_4(out_4[12]));
  mux2x1 mux2x1_14 (.A(in_2[13]), .B(in_3[13]), .S(in_1), .out_4(out_4[13]));
  mux2x1 mux2x1_15 (.A(in_2[14]), .B(in_3[14]), .S(in_1), .out_4(out_4[14]));
  mux2x1 mux2x1_16 (.A(in_2[15]), .B(in_3[15]), .S(in_1), .out_4(out_4[15]));
endmodule

module ZEXT_8to16 (
  input  [7:0] in_1,
  output [15:0] out_2
);


  assign out_2 = {{8{1'b0}}, in_1};
endmodule

module SEXT_11to16 (
  input  [10:0] in_1,
  output [15:0] out_2
);


  assign out_2 = {{6{in_1[10]}}, in_1[9:0]};

  // Notes on the sheet:
  //   11 bit Sign ext
endmodule

module SEXT_9to16 (
  input  [8:0] in_1,
  output [15:0] out_2
);


  assign out_2 = {{8{in_1[8]}}, in_1[7:0]};
endmodule

module SEXT_6to16 (
  input  [5:0] in_1,
  output [15:0] out_2
);


  assign out_2 = {{11{in_1[5]}}, in_1[4:0]};
endmodule

module SEXT_5to16 (
  input  [4:0] in_1,
  output [15:0] out_2
);


  assign out_2 = {{12{in_1[4]}}, in_1[3:0]};
endmodule

module fullAdder (
  input  [15:0] A,
  input  [15:0] B,
  output [15:0] R
);

  Adder16Bits adder16bits_1 (.A(A), .B(B), .Sum(R));  // open: C_Out, penult_carry_out
endmodule

module plus1 (
  input  [15:0] in_1,
  output [15:0] out_2
);

  Adder16Bits adder16bits_1 (.A(in_1), .B(16'h1), .Sum(out_2));  // open: C_Out, penult_carry_out
endmodule

module ALU (
  input  [15:0] A,
  input  [15:0] B,
  input  [1:0] Selector,
  output [15:0] Result
);

  wire [15:0] adder16bits_1_sum, and16bitwise_1_r, not16bitwise_1_r;

  Adder16Bits adder16bits_1 (.A(A), .B(B), .Sum(adder16bits_1_sum));  // open: C_Out, penult_carry_out
  AND16Bitwise and16bitwise_1 (.A(A), .B(B), .R(and16bitwise_1_r));
  Multiplexer #(.select(2), .width(16)) multiplexer_1 (
    .in0(adder16bits_1_sum), .in1(and16bitwise_1_r), .in2(not16bitwise_1_r), .in3(A), .out(Result),
    .sel(Selector));
  NOT16Bitwise not16bitwise_1 (.A(A), .R(not16bitwise_1_r));

  // Notes on the sheet:
  //   3 :A
  //   0 : Suma
  //   1 : AND bitwise
  //   2 :NOT A
endmodule

module \logic  (
  input  [15:0] in_1,
  output P,
  output Z,
  output N
);

  Comparator16Bit comparator16bit_1 (.A(in_1), .B({16{1'b0}}), .Less(N), .Great(P), .Equal(Z));
endmodule

module fileRegister (
  input  [15:0] DIN,
  input  [2:0] DR,
  input  LDREG,
  input  CLK,
  input  RES,
  input  [2:0] SR1,
  input  [2:0] SR2,
  output [15:0] R0,
  output [15:0] R1,
  output [15:0] R2,
  output [15:0] R3,
  output [15:0] R4,
  output [15:0] R5,
  output [15:0] R6,
  output [15:0] R7,
  output [15:0] SR1OUT,
  output [15:0] SR2OUT
);

  wire and_1_out, and_2_out, and_3_out, and_4_out, and_5_out, and_6_out, and_7_out, and_8_out,
       decoder_1_out0, decoder_1_out1, decoder_1_out2, decoder_1_out3, decoder_1_out4, decoder_1_out5,
       decoder_1_out6, decoder_1_out7;

  Decoder #(.select(3)) decoder_1 (
    .out0(decoder_1_out0), .out1(decoder_1_out1), .out2(decoder_1_out2), .out3(decoder_1_out3),
    .out4(decoder_1_out4), .out5(decoder_1_out5), .out6(decoder_1_out6), .out7(decoder_1_out7), .sel(DR));  // open: en
  and and_1 (and_1_out, decoder_1_out0, LDREG);
  and and_2 (and_2_out, decoder_1_out1, LDREG);
  and and_3 (and_3_out, decoder_1_out2, LDREG);
  and and_4 (and_4_out, decoder_1_out3, LDREG);
  and and_5 (and_5_out, decoder_1_out4, LDREG);
  and and_6 (and_6_out, decoder_1_out5, LDREG);
  and and_7 (and_7_out, decoder_1_out6, LDREG);
  and and_8 (and_8_out, decoder_1_out7, LDREG);
  Register #(.width(16)) register_1 (.D(DIN), .en(and_1_out), .clk(CLK), .Q(R0), .clr(RES));
  Register #(.width(16)) register_2 (.D(DIN), .en(and_2_out), .clk(CLK), .Q(R1), .clr(RES));
  Register #(.width(16)) register_3 (.D(DIN), .en(and_3_out), .clk(CLK), .Q(R2), .clr(RES));
  Register #(.width(16)) register_4 (.D(DIN), .en(and_4_out), .clk(CLK), .Q(R3), .clr(RES));
  Register #(.width(16)) register_5 (.D(DIN), .en(and_5_out), .clk(CLK), .Q(R4), .clr(RES));
  Register #(.width(16)) register_6 (.D(DIN), .en(and_6_out), .clk(CLK), .Q(R5), .clr(RES));
  Register #(.width(16)) register_7 (.D(DIN), .en(and_7_out), .clk(CLK), .Q(R6), .clr(RES));
  Register #(.width(16)) register_8 (.D(DIN), .en(and_8_out), .clk(CLK), .Q(R7), .clr(RES));
  Multiplexer #(.select(3), .width(16)) multiplexer_1 (
    .in0(R0), .in1(R1), .in2(R2), .in3(R3), .in4(R4), .in5(R5), .in6(R6), .in7(R7), .out(SR2OUT), .sel(SR2));
  Multiplexer #(.select(3), .width(16)) multiplexer_2 (
    .in0(R0), .in1(R1), .in2(R2), .in3(R3), .in4(R4), .in5(R5), .in6(R6), .in7(R7), .out(SR1OUT), .sel(SR1));
endmodule

module MAR_reg (
  input  [15:0] MAR_IN,
  input  LD_MAR,
  input  CLK,
  input  RES,
  output [15:0] MAR_OUT
);

  Register #(.width(16)) register_1 (.D(MAR_IN), .en(LD_MAR), .clk(CLK), .Q(MAR_OUT), .clr(RES));
endmodule

module IR_Register (
  input  [15:0] IR_IN,
  input  LD_IR,
  input  CLK,
  input  RES,
  output [15:0] IR_OUT
);

  Register #(.width(16)) register_1 (.D(IR_IN), .en(LD_IR), .clk(CLK), .Q(IR_OUT), .clr(RES));
endmodule

module MDR_reg (
  input  [15:0] MDR_IN,
  input  LD_MDR,
  input  CLK,
  input  RES,
  output [15:0] MDR_OUT
);

  Register #(.width(16)) register_1 (.D(MDR_IN), .en(LD_MDR), .clk(CLK), .Q(MDR_OUT), .clr(RES));
endmodule

module PC_reg (
  input  [15:0] DIN,
  input  RES,
  input  LDPC,
  input  CLK,
  output [15:0] out_5
);

  wire or_1_out;
  wire [15:0] multiplexer_1_out;

  or or_1 (or_1_out, RES, LDPC);
  Multiplexer #(.width(16)) multiplexer_1 (.in0(DIN), .in1(16'h3000), .out(multiplexer_1_out), .sel(RES));
  Register #(.width(16)) register_1 (.D(multiplexer_1_out), .en(or_1_out), .clk(CLK), .Q(out_5), .clr(1'b0));
endmodule

module UC (
  input  INT,
  input  R,
  input  BEN,
  input  PSR15,
  input  [4:0] IR15_11,
  input  CLK,
  input  RES,
  input  IR5,
  output [5:0] NSN,
  output [5:0] CSN,
  output [41:0] out_11
);

  wire and_1_out, and_2_out, and_3_out, and_4_out, and_5_out, COND0, COND1, COND2, IRD, J0, J1, J2, J3, J4,
       J5;
  wire [4:0] or_5_out;
  wire [5:0] multiplexer_1_out;
  wire [51:0] rom_1_data;

  and and_1 (and_1_out, COND2, ~COND1, COND0, INT);  // AND_Gate
  or or_1 (or_5_out[4], J4, and_1_out);
  and and_2 (and_2_out, COND2, ~COND1, ~COND0, PSR15);  // AND_Gate
  or or_2 (or_5_out[3], J3, and_2_out);
  Multiplexer #(.width(6)) multiplexer_1 (
    .in0({J5, or_5_out}), .in1({2'b00, IR15_11[4:1]}), .out(multiplexer_1_out), .sel(IRD));
  and and_3 (and_3_out, ~COND2, COND1, ~COND0, BEN);  // AND_Gate
  or or_3 (or_5_out[2], J2, and_3_out);
  Multiplexer #(.width(6)) multiplexer_2 (.in0(multiplexer_1_out), .in1(6'b010010), .out(NSN), .sel(RES));
  ROM #(.addrWidth(6), .dataWidth(52)) rom_1 (.addr(NSN), .data(rom_1_data));
  and and_4 (and_4_out, ~COND2, ~COND1, COND0, R);  // AND_Gate
  or or_4 (or_5_out[1], J1, and_4_out);
  and and_5 (and_5_out, ~COND2, COND1, COND0, IR15_11[0]);  // AND_Gate
  or or_5 (or_5_out[0], J0, and_5_out);
  Register #(.width(6)) CSNumber (.D(NSN), .en(1'b1), .Q(CSN), .clk(CLK), .clr(1'b0));
  // NoConnect on rom_1_data[1]
  Register #(.width(52)) register_1 (
    .D({rom_1_data[51:2], IR5, rom_1_data[0]}), .en(1'b1), .clk(CLK),
    .Q({IRD, COND2, COND1, COND0, J5, J4, J3, J2, J1, J0, out_11}), .clr(1'b0));

  // Other names for the same wires on the sheet: IR15_12[3:0] = IR15_11[4:1]; IR11 = IR15_11[0]

  // Notes on the sheet:
  //   Interruption
  //   User Privilege Mode
  //   NEXT STATE NUMBER
  //   Branch
  //   contents of rom_1 (hex, n*v repeats v):
  //   2480000000000 483008010000 660004004400 5e0004004400 3502020040000 483008010020 66000401a420
  //   5e000401a420 4920008020060 483008010040 620004014420 760004014420 480800218000 4950480800200
  //   483004004400 720004000000 1400000000018 0 5860820000000 0 480800218000 480800206000 480800204000
  //   410008000060 1610000000010 1650000000010 660010000000 483010000000 1712020040010 1750000000010
  //   480810100000 5e0010000000 8004000000000 1850000000010 4cc20004a0800 808010000000 1910000000010
  //   a620004a1000 9c0810100000 a220004a0800 1a10000000010 1a40000000018 881450000080 bd0001000000
  //   b50480800100 9421004a1800 0 c220004a1000 1c00000000018 49504c0800000 d20002000000 480000000000
  //   1d10000000010 0 480810100000 4*0 4822004a0000
  //   Memory Ready
  //   Addressing Mode
  //   NEXT STATE
  //   CURRENT STATE
endmodule

module BEN_reg (
  input  D,
  input  LD,
  input  CLK,
  input  RESET,
  output Q
);

  Register #(.width(1)) register_1 (.D(D), .en(LD), .clk(CLK), .Q(Q), .clr(RESET));
endmodule

module memory (
  input  [15:0] ADDRESS,
  input  CLK,
  input  RES,
  input  [15:0] DATO,
  input  RW,
  input  MEMEN,
  input  MIOEN,
  output [15:0] MEM_OUT,
  output R
);

  wire and_1_out, and_2_out, and_3_out, counter_1_carry, not_1_out, undriven;
  wire [1:0] counter_1_q, undriven_2;

  not not_1 (not_1_out, RW);
  and and_1 (and_1_out, MEMEN, RW);
  and and_2 (and_2_out, MEMEN, not_1_out);
  // Probe on DATO
  RAM #(.addrWidth(16), .dataWidth(16)) ram_1 (
    .addr(ADDRESS), .we(and_1_out), .oe(and_2_out), .clk(CLK), .din(DATO), .dout(MEM_OUT));
  // NoConnect on undriven
  // NoConnect on undriven_2
  // NoConnect on counter_1_q
  Counter #(.max('h2), .width(2)) counter_1 (
    .load(undriven), .D(undriven_2), .count(MEMEN), .Q(counter_1_q), .carry(counter_1_carry), .up(1'b1),
    .clk(CLK), .clr(RES));
  and and_3 (and_3_out, MIOEN, ~MEMEN);  // AND_Gate
  // Probe on counter_1_carry
  or or_1 (R, counter_1_carry, and_3_out);
endmodule

module NZP_reg (
  input  P_IN,
  input  Z_IN,
  input  N_IN,
  input  LD,
  input  CLK,
  input  RESET,
  output N,
  output Z,
  output P
);

  Register #(.width(1)) register_1 (.D(N_IN), .en(LD), .clk(CLK), .Q(N), .clr(LD));
  Register #(.width(1)) register_2 (.D(Z_IN), .en(LD), .clk(CLK), .Q(Z), .clr(LD));
  Register #(.width(1)) register_3 (.D(P_IN), .en(LD), .clk(CLK), .Q(P), .clr(LD));

  assign RESET = LD;
endmodule

module PC_mux (
  input  [1:0] Control,
  input  [15:0] In1,
  input  [15:0] In2,
  input  [15:0] In3,
  output [15:0] out_5
);

  mux4x1_16Bits mux4x1_16bits_1 (.in_4(In3), .in_3(In2), .in_1(Control), .in_2(In1), .out_6(out_5));  // open: in_5
endmodule

module SR2_mux (
  input  Control,
  input  [15:0] In1,
  input  [15:0] In2,
  output [15:0] mux_out
);

  mux2x1_16Bits mux2x1_16bits_1 (.in_2(In1), .in_3(In2), .in_1(Control), .out_4(mux_out));
endmodule

module mar_mux (
  input  Control,
  input  [15:0] In1,
  input  [15:0] In2,
  output [15:0] mux_out
);

  mux2x1_16Bits mux2x1_16bits_1 (.in_2(In1), .in_3(In2), .in_1(Control), .out_4(mux_out));
endmodule

module addr2_mux (
  input  [1:0] in_1,
  input  [15:0] In1,
  input  [15:0] In2,
  input  [15:0] In3,
  input  [15:0] In4,
  output [15:0] out_6
);

  mux4x1_16Bits mux4x1_16bits_1 (.in_5(In4), .in_4(In3), .in_3(In2), .in_1(in_1), .in_2(In1), .out_6(out_6));
endmodule
